// Logisim project 16bCPUv2.circ as structural Verilog: 46 circuits, main circuit testall_wlogic_V2
module Mux_2to1 (
  input  A0,
  input  B0,
  input  Sel,
  output O0
);

  wire and_1_out, and_2_out, not_1_out;

  not not_1 (not_1_out, Sel);
  and and_1 (and_1_out, A0, not_1_out);
  and and_2 (and_2_out, B0, Sel);
  or or_1 (O0, and_1_out, and_2_out);
endmodule

module Mux_4to1 (
  input  A,
  input  B,
  input  C,
  input  D,
  input  Sel1,
  input  Sel0,
  output Y
);

  wire mux1_o0, mux2_o0;

  Mux_2to1 mux1 (.Sel(Sel0), .A0(A), .B0(B), .O0(mux1_o0));
  Mux_2to1 mux2 (.Sel(Sel0), .A0(C), .B0(D), .O0(mux2_o0));
  Mux_2to1 mux3 (.Sel(Sel1), .A0(mux1_o0), .B0(mux2_o0), .O0(Y));

  // Notes on the sheet:
  //   A or B
  //   C or D
  //   mux1 or mux2
endmodule

module inverting_tristate_buffer_1bit (
  input  D,
  input  OE,
  output Y
);

  wire not_1_out, transistor_1_out, transistor_4_out;

  not not_1 (not_1_out, OE);
  Transistor transistor_1 (.in(1'b1), .out(transistor_1_out), .gate(not_1_out));
  Transistor transistor_2 (.in(transistor_1_out), .out(Y), .gate(D));
  Transistor #(.\type ("n")) transistor_3 (.in(transistor_4_out), .out(Y), .gate(D));
  Transistor #(.\type ("n")) transistor_4 (.in(1'b0), .out(transistor_4_out), .gate(OE));
endmodule

module noninverting_tristate_buffer_1bit (
  input  OE,
  input  D,
  output Y
);

  wire not_1_out;

  not not_1 (not_1_out, D);
  inverting_tristate_buffer_1bit inverting_tristate_buffer_1bit_1 (.D(not_1_out), .OE(OE), .Y(Y));
endmodule

module TrisBuf_1w (
  input  OE,
  input  [15:0] D,
  output [15:0] Y
);

  noninverting_tristate_buffer_1bit noninverting_tristate_buffer_1bit_1 (.OE(OE), .D(D[0]), .Y(Y[0]));
  noninverting_tristate_buffer_1bit noninverting_tristate_buffer_1bit_2 (.OE(OE), .D(D[1]), .Y(Y[1]));
  noninverting_tristate_buffer_1bit noninverting_tristate_buffer_1bit_3 (.OE(OE), .D(D[2]), .Y(Y[2]));
  noninverting_tristate_buffer_1bit noninverting_tristate_buffer_1bit_4 (.OE(OE), .D(D[3]), .Y(Y[3]));
  noninverting_tristate_buffer_1bit noninverting_tristate_buffer_1bit_5 (.OE(OE), .D(D[4]), .Y(Y[4]));
  noninverting_tristate_buffer_1bit noninverting_tristate_buffer_1bit_6 (.OE(OE), .D(D[5]), .Y(Y[5]));
  noninverting_tristate_buffer_1bit noninverting_tristate_buffer_1bit_7 (.OE(OE), .D(D[6]), .Y(Y[6]));
  noninverting_tristate_buffer_1bit noninverting_tristate_buffer_1bit_8 (.OE(OE), .D(D[7]), .Y(Y[7]));
  noninverting_tristate_buffer_1bit noninverting_tristate_buffer_1bit_9 (.OE(OE), .D(D[8]), .Y(Y[8]));
  noninverting_tristate_buffer_1bit noninverting_tristate_buffer_1bit_10 (.OE(OE), .D(D[9]), .Y(Y[9]));
  noninverting_tristate_buffer_1bit noninverting_tristate_buffer_1bit_11 (.OE(OE), .D(D[10]), .Y(Y[10]));
  noninverting_tristate_buffer_1bit noninverting_tristate_buffer_1bit_12 (.OE(OE), .D(D[11]), .Y(Y[11]));
  noninverting_tristate_buffer_1bit noninverting_tristate_buffer_1bit_13 (.OE(OE), .D(D[12]), .Y(Y[12]));
  noninverting_tristate_buffer_1bit noninverting_tristate_buffer_1bit_14 (.OE(OE), .D(D[13]), .Y(Y[13]));
  noninverting_tristate_buffer_1bit noninverting_tristate_buffer_1bit_15 (.OE(OE), .D(D[14]), .Y(Y[14]));
  noninverting_tristate_buffer_1bit noninverting_tristate_buffer_1bit_16 (.OE(OE), .D(D[15]), .Y(Y[15]));
endmodule

module D_latch_sClr (
  input  EN,
  input  D,
  input  sCLR_b,
  output Q,
  output Q_b
);

  wire and_1_out, and_2_out, and_3_out, not_1_out;

  and and_1 (and_1_out, D, sCLR_b);
  not not_1 (not_1_out, and_1_out);
  and and_2 (and_2_out, not_1_out, EN);
  and and_3 (and_3_out, EN, and_1_out);
  nor nor_1 (Q, and_2_out, Q_b);
  nor nor_2 (Q_b, Q, and_3_out);

  // Notes on the sheet:
  //   R
  //   S
  //   for SR latch ==>
  //   R S     Q
  //   0 1      1
  //   1 0      0
  //   for D latch ==>
  //   0 0 is memory
  //   1 1 is forbidden
  //   En=0 gives memory state
  //   En=1 Sets or Resets Q
endmodule

module D_flipflop_sClr (
  input  sCLR_b,
  input  D,
  input  clk,
  output Q,
  output Q_b
);

  wire latch1_q, latch1_q_b, not_1_out;

  D_latch_sClr latch1 (.D(D), .sCLR_b(sCLR_b), .EN(not_1_out), .Q(latch1_q), .Q_b(latch1_q_b));
  D_latch_sClr latch2 (.D(latch1_q), .sCLR_b(1'b1), .EN(clk), .Q(Q), .Q_b(Q_b));
  // NoConnect on latch1_q_b
  not not_1 (not_1_out, clk);

  // Notes on the sheet:
  //   when clk <= '1
  //   when clk <= '0
  //   latch1 is memory
  //   latch2 is transparent
  //   other way round
endmodule

module D_flipflop_sClr_en (
  input  CLR,
  input  D,
  input  en,
  input  clk,
  output Q,
  output Q_b
);

  wire mux_2to1_1_o0;

  Mux_2to1 mux_2to1_1 (.Sel(en), .A0(Q), .B0(D), .O0(mux_2to1_1_o0));
  D_flipflop_sClr dff (.D(mux_2to1_1_o0), .clk(clk), .sCLR_b(CLR), .Q(Q), .Q_b(Q_b));

  // Notes on the sheet:
  //   sCLR
  //   D_ff
  //   Q_ff
  //   D_ff <= Q_ff if en=0
  //   D_ff <= D if en=1
  //   sCLR is synchronous & active low
endmodule

module JK_latch (
  input  J,
  input  en,
  input  K,
  output Q,
  output Q_b
);

  wire and_1_out, and_2_out;

  and and_1 (and_1_out, Q_b, J, en);
  and and_2 (and_2_out, en, K, Q);
  nor nor_1 (Q, and_2_out, Q_b);
  nor nor_2 (Q_b, Q, and_1_out);

  // Notes on the sheet:
  //   warning : J='1, K='1, wil turn to oscillate
  //   j  k    Q
  //   1  0  set
  //   0  1  reset
  //   1  1  toogle infinitely
  //   0  0  memory
endmodule

module JK_flipflop (
  input  sCLR_b,
  input  J,
  input  K,
  input  clk,
  output Q,
  output Q_b
);

  wire and_1_out, and_2_out, and_3_out, and_4_out, noninverting_tristate_buffer_1bit_1_y,
       noninverting_tristate_buffer_1bit_2_y, nor_1_out, nor_2_out, nor_3_out, nor_4_out, not_1_out,
       not_2_out;

  noninverting_tristate_buffer_1bit noninverting_tristate_buffer_1bit_1 (
    .OE(sCLR_b), .D(J), .Y(noninverting_tristate_buffer_1bit_1_y));
  noninverting_tristate_buffer_1bit noninverting_tristate_buffer_1bit_2 (
    .OE(not_2_out), .D(noninverting_tristate_buffer_1bit_1_y), .Y(noninverting_tristate_buffer_1bit_2_y));
  noninverting_tristate_buffer_1bit noninverting_tristate_buffer_1bit_3 (
    .OE(sCLR_b), .D(K), .Y(noninverting_tristate_buffer_1bit_2_y));
  not not_1 (not_1_out, clk);
  and and_1 (and_1_out, Q_b, noninverting_tristate_buffer_1bit_1_y, not_1_out);
  and and_2 (and_2_out, not_1_out, noninverting_tristate_buffer_1bit_2_y, Q);
  nor nor_1 (nor_1_out, and_2_out, nor_2_out);
  nor nor_2 (nor_2_out, nor_1_out, and_1_out);
  and and_3 (and_3_out, nor_2_out, clk);
  and and_4 (and_4_out, clk, nor_1_out);
  not not_2 (not_2_out, sCLR_b);
  nor nor_3 (nor_3_out, and_3_out, Q_b);
  noninverting_tristate_buffer_1bit noninverting_tristate_buffer_1bit_4 (.OE(sCLR_b), .D(nor_3_out), .Y(Q));
  nor nor_4 (nor_4_out, Q, and_4_out);
  noninverting_tristate_buffer_1bit noninverting_tristate_buffer_1bit_5 (.OE(sCLR_b), .D(nor_4_out), .Y(Q_b));

  // Notes on the sheet:
  //   when sCLR_b is '1 ==>
  //   Q
  //   j  k    Q
  //   1  0  set
  //   0  1  reset
  //   1  1  toogle
  //   0  0  memory
  //   S
  //   SR latch transparent when clk is high
endmodule

module program_counter_4b (
  input  COUNTEN,
  input  sRst_b,
  input  clk,
  input  LOADEN,
  input  [3:0] L_s,
  output rcOut,
  output [3:0] cOut_s
);

  wire c0_q_b, c1_q_b, c2_q_b, c3_q_b, count_or_load_y, mux_2to1_1_o0, noninverting_tristate_buffer_1bit_1_y,
       noninverting_tristate_buffer_1bit_2_y, noninverting_tristate_buffer_1bit_4_y,
       noninverting_tristate_buffer_1bit_6_y, noninverting_tristate_buffer_1bit_7_y,
       noninverting_tristate_buffer_1bit_8_y, not_1_out, reset_y, t1_out, t2_out, t3_out;

  Mux_2to1 mux_2to1_1 (.Sel(COUNTEN), .A0(1'b0), .B0(1'b1), .O0(mux_2to1_1_o0));
  not not_1 (not_1_out, LOADEN);
  noninverting_tristate_buffer_1bit reset (.OE(LOADEN), .D(L_s[0]), .Y(reset_y));
  noninverting_tristate_buffer_1bit notransmit_if_load (.OE(not_1_out), .D(mux_2to1_1_o0), .Y(reset_y));
  noninverting_tristate_buffer_1bit count_or_load (.OE(not_1_out), .D(reset_y), .Y(count_or_load_y));
  inverting_tristate_buffer_1bit set (.D(L_s[0]), .OE(LOADEN), .Y(count_or_load_y));
  and t1 (t1_out, mux_2to1_1_o0, cOut_s[0]);
  noninverting_tristate_buffer_1bit noninverting_tristate_buffer_1bit_1 (
    .OE(not_1_out), .D(t1_out), .Y(noninverting_tristate_buffer_1bit_1_y));
  jk_flipflop_V2 c0 (.J(reset_y), .K(count_or_load_y), .clk(clk), .sRst_b(sRst_b), .Q(cOut_s[0]), .Q_b(c0_q_b));
  // NoConnect on c0_q_b
  noninverting_tristate_buffer_1bit noninverting_tristate_buffer_1bit_2 (
    .OE(not_1_out), .D(noninverting_tristate_buffer_1bit_1_y), .Y(noninverting_tristate_buffer_1bit_2_y));
  noninverting_tristate_buffer_1bit noninverting_tristate_buffer_1bit_3 (
    .OE(LOADEN), .D(L_s[1]), .Y(noninverting_tristate_buffer_1bit_1_y));
  jk_flipflop_V2 c1 (
    .J(noninverting_tristate_buffer_1bit_1_y), .K(noninverting_tristate_buffer_1bit_2_y), .clk(clk),
    .sRst_b(sRst_b), .Q(cOut_s[1]), .Q_b(c1_q_b));
  // NoConnect on c1_q_b
  inverting_tristate_buffer_1bit inverting_tristate_buffer_1bit_1 (
    .D(L_s[1]), .OE(LOADEN), .Y(noninverting_tristate_buffer_1bit_2_y));
  noninverting_tristate_buffer_1bit noninverting_tristate_buffer_1bit_4 (
    .OE(LOADEN), .D(L_s[2]), .Y(noninverting_tristate_buffer_1bit_4_y));
  and t2 (t2_out, mux_2to1_1_o0, t1_out, cOut_s[1]);
  noninverting_tristate_buffer_1bit noninverting_tristate_buffer_1bit_5 (
    .OE(not_1_out), .D(t2_out), .Y(noninverting_tristate_buffer_1bit_4_y));
  noninverting_tristate_buffer_1bit noninverting_tristate_buffer_1bit_6 (
    .OE(not_1_out), .D(noninverting_tristate_buffer_1bit_4_y), .Y(noninverting_tristate_buffer_1bit_6_y));
  inverting_tristate_buffer_1bit inverting_tristate_buffer_1bit_2 (
    .D(L_s[2]), .OE(LOADEN), .Y(noninverting_tristate_buffer_1bit_6_y));
  and t3 (t3_out, mux_2to1_1_o0, t2_out, cOut_s[2]);
  noninverting_tristate_buffer_1bit noninverting_tristate_buffer_1bit_7 (
    .OE(not_1_out), .D(t3_out), .Y(noninverting_tristate_buffer_1bit_7_y));
  jk_flipflop_V2 c2 (
    .J(noninverting_tristate_buffer_1bit_4_y), .K(noninverting_tristate_buffer_1bit_6_y), .clk(clk),
    .sRst_b(sRst_b), .Q(cOut_s[2]), .Q_b(c2_q_b));
  // NoConnect on c2_q_b
  noninverting_tristate_buffer_1bit noninverting_tristate_buffer_1bit_8 (
    .OE(not_1_out), .D(noninverting_tristate_buffer_1bit_7_y), .Y(noninverting_tristate_buffer_1bit_8_y));
  inverting_tristate_buffer_1bit inverting_tristate_buffer_1bit_3 (
    .D(L_s[3]), .OE(LOADEN), .Y(noninverting_tristate_buffer_1bit_8_y));
  noninverting_tristate_buffer_1bit noninverting_tristate_buffer_1bit_9 (
    .OE(LOADEN), .D(L_s[3]), .Y(noninverting_tristate_buffer_1bit_7_y));
  jk_flipflop_V2 c3 (
    .J(noninverting_tristate_buffer_1bit_7_y), .K(noninverting_tristate_buffer_1bit_8_y), .clk(clk),
    .sRst_b(sRst_b), .Q(cOut_s[3]), .Q_b(c3_q_b));
  // NoConnect on c3_q_b
  and and_1 (rcOut, cOut_s[0], cOut_s[1], cOut_s[2], cOut_s[3]);

  // Notes on the sheet:
  //   b0
  //   b1
  //   b2
  //   b3
  //   t0
  //   L0
  //   L1
  //   L2
  //   L3
  //   count_or_load : count if '1, else load
endmodule

module jk_flipflop_V2 (
  input  sRst_b,
  input  J,
  input  K,
  input  clk,
  output Q,
  output Q_b
);

  wire and_1_out, and_2_out, or_1_out;

  and and_1 (and_1_out, Q_b, J);
  and and_2 (and_2_out, ~K, Q);  // AND_Gate
  or or_1 (or_1_out, and_1_out, and_2_out);
  D_flipflop_sClr d_flipflop_sclr_1 (.D(or_1_out), .clk(clk), .sCLR_b(sRst_b), .Q(Q), .Q_b(Q_b));
endmodule

module sram_cell (
  input  RE,
  input  WE_b,
  input  wrote_bit,
  output read_bit
);

  wire controlled_buffer_1_out, not_1_out, not_2_out;

  not not_1 (not_1_out, WE_b);
  assign controlled_buffer_1_out = not_1_out ? wrote_bit : 1'bz;  // Controlled_Buffer controlled_buffer_1
  assign controlled_buffer_1_out = WE_b ? ~not_2_out : 1'bz;  // Controlled_Inverter controlled_inverter_1
  not not_2 (not_2_out, controlled_buffer_1_out);
  assign read_bit = RE ? ~not_2_out : 1'bz;  // Controlled_Inverter controlled_inverter_2

  // Notes on the sheet:
  //   RE: initial=0x1
  //   acts as a buffer on bitline
  //   2x tampon : pareil que pour regF_cell,
  //   Dissocier stored de wrote_bit le td suivant.
  //   if any RE or WE is asserted, action will occur on low phase of clk
  //   stored
  //   réactiver le feedback PENDANT que le fil stored est encore drivé par wrote_bit.
  //   since bus aren't bidir in Logisim, both can be asserted at the same time without issue.
  //   !stored
endmodule

module Dec_4to16 (
  input  b3,
  input  b2,
  input  b1,
  input  b0,
  input  EN,
  output [15:0] Line_s
);

  wire not_1_out, not_2_out, not_3_out, not_4_out;

  not not_1 (not_1_out, b3);
  not not_2 (not_2_out, b2);
  not not_3 (not_3_out, b1);
  not not_4 (not_4_out, b0);
  and and_1 (Line_s[0], not_4_out, not_3_out, EN, not_2_out, not_1_out);
  and and_2 (Line_s[1], b0, not_3_out, EN, not_2_out, not_1_out);
  and and_3 (Line_s[2], not_4_out, b1, EN, not_2_out, not_1_out);
  and and_4 (Line_s[3], b0, b1, EN, not_2_out, not_1_out);
  and and_5 (Line_s[4], not_4_out, not_3_out, EN, b2, not_1_out);
  and and_6 (Line_s[5], b0, not_3_out, EN, b2, not_1_out);
  and and_7 (Line_s[6], not_4_out, b1, EN, b2, not_1_out);
  and and_8 (Line_s[7], b0, b1, EN, b2, not_1_out);
  and and_9 (Line_s[8], not_4_out, not_3_out, EN, not_2_out, b3);
  and and_10 (Line_s[9], b0, not_3_out, EN, not_2_out, b3);
  and and_11 (Line_s[10], not_4_out, b1, EN, not_2_out, b3);
  and and_12 (Line_s[11], b0, b1, EN, not_2_out, b3);
  and and_13 (Line_s[12], not_4_out, not_3_out, EN, b2, b3);
  and and_14 (Line_s[13], b0, not_3_out, EN, b2, b3);
  and and_15 (Line_s[14], not_4_out, b1, EN, b2, b3);
  and and_16 (Line_s[15], b0, b1, EN, b2, b3);

  // Notes on the sheet:
  //   one could en AFTER pdelay time to ensure decoded line is VALID
endmodule

module sram_1w (
  input  wordline,
  input  [15:0] wb_s,
  input  R_or_W_b,
  output [15:0] rb_s
);

  wire and_1_out, or_1_out;
  wire [15:0] buffer_1_out;

  or or_1 (or_1_out, ~wordline, R_or_W_b);  // OR_Gate
  and and_1 (and_1_out, wordline, R_or_W_b);
  sram_cell sram_cell_1 (.RE(and_1_out), .WE_b(or_1_out), .wrote_bit(buffer_1_out[15]), .read_bit(rb_s[15]));
  sram_cell sram_cell_2 (.RE(and_1_out), .WE_b(or_1_out), .wrote_bit(buffer_1_out[14]), .read_bit(rb_s[14]));
  sram_cell sram_cell_3 (.RE(and_1_out), .WE_b(or_1_out), .wrote_bit(buffer_1_out[13]), .read_bit(rb_s[13]));
  sram_cell sram_cell_4 (.RE(and_1_out), .WE_b(or_1_out), .wrote_bit(buffer_1_out[12]), .read_bit(rb_s[12]));
  assign buffer_1_out = wb_s;  // Buffer buffer_1, 16 bits wide
  sram_cell sram_cell_5 (.RE(and_1_out), .WE_b(or_1_out), .wrote_bit(buffer_1_out[11]), .read_bit(rb_s[11]));
  sram_cell sram_cell_6 (.RE(and_1_out), .WE_b(or_1_out), .wrote_bit(buffer_1_out[10]), .read_bit(rb_s[10]));
  sram_cell sram_cell_7 (.RE(and_1_out), .WE_b(or_1_out), .wrote_bit(buffer_1_out[9]), .read_bit(rb_s[9]));
  sram_cell sram_cell_8 (.RE(and_1_out), .WE_b(or_1_out), .wrote_bit(buffer_1_out[8]), .read_bit(rb_s[8]));
  sram_cell sram_cell_9 (.RE(and_1_out), .WE_b(or_1_out), .wrote_bit(buffer_1_out[7]), .read_bit(rb_s[7]));
  sram_cell sram_cell_10 (.RE(and_1_out), .WE_b(or_1_out), .wrote_bit(buffer_1_out[6]), .read_bit(rb_s[6]));
  sram_cell sram_cell_11 (.RE(and_1_out), .WE_b(or_1_out), .wrote_bit(buffer_1_out[5]), .read_bit(rb_s[5]));
  sram_cell sram_cell_12 (.RE(and_1_out), .WE_b(or_1_out), .wrote_bit(buffer_1_out[4]), .read_bit(rb_s[4]));
  sram_cell sram_cell_13 (.RE(and_1_out), .WE_b(or_1_out), .wrote_bit(buffer_1_out[3]), .read_bit(rb_s[3]));
  sram_cell sram_cell_14 (.RE(and_1_out), .WE_b(or_1_out), .wrote_bit(buffer_1_out[2]), .read_bit(rb_s[2]));
  sram_cell sram_cell_15 (.RE(and_1_out), .WE_b(or_1_out), .wrote_bit(buffer_1_out[1]), .read_bit(rb_s[1]));
  sram_cell sram_cell_16 (.RE(and_1_out), .WE_b(or_1_out), .wrote_bit(buffer_1_out[0]), .read_bit(rb_s[0]));

  // Notes on the sheet:
  //   add delay to ensure wb_s hasnt changed by the time each cell locks on (from !we=0->1)
endmodule

module sram_16w (
  input  [15:0] wb_s,
  input  INIT,
  input  R_or_W_b,
  input  addr_valid,
  input  CE,
  input  [3:0] addr4b_s,
  output [15:0] rb_s
);

  wire and_1_out, and_2_out, and_3_out, and_4_out, and_5_out, and_6_out, and_7_out, and_8_out, and_9_out,
       and_10_out, and_11_out, and_12_out, and_13_out, and_14_out, and_15_out, and_16_out, and_17_out,
       and_18_out, not_1_out, not_2_out, or_1_out;
  wire [15:0] controlled_buffer_1_out, dec_4to16_1_line_s;

  not not_1 (not_1_out, INIT);
  or or_1 (or_1_out, addr_valid, INIT);
  and and_1 (and_1_out, not_1_out, CE);
  assign controlled_buffer_1_out = not_1_out ? dec_4to16_1_line_s : 16'bz;  // Controlled_Buffer controlled_buffer_1
  Dec_4to16 dec_4to16_1 (
    .b2(addr4b_s[2]), .b1(addr4b_s[1]), .b0(addr4b_s[0]), .EN(and_1_out), .b3(addr4b_s[3]),
    .Line_s(dec_4to16_1_line_s));
  not not_2 (not_2_out, not_1_out);
  assign controlled_buffer_1_out = not_2_out ? ~{16{1'b0}} : 16'bz;  // Controlled_Inverter controlled_inverter_1
  and and_2 (and_2_out, controlled_buffer_1_out[0], or_1_out);
  and and_3 (and_3_out, controlled_buffer_1_out[1], or_1_out);
  and and_4 (and_4_out, controlled_buffer_1_out[2], or_1_out);
  and and_5 (and_5_out, controlled_buffer_1_out[3], or_1_out);
  and and_6 (and_6_out, controlled_buffer_1_out[4], or_1_out);
  and and_7 (and_7_out, controlled_buffer_1_out[5], or_1_out);
  and and_8 (and_8_out, controlled_buffer_1_out[6], or_1_out);
  and and_9 (and_9_out, controlled_buffer_1_out[7], or_1_out);
  and and_10 (and_10_out, controlled_buffer_1_out[8], or_1_out);
  and and_11 (and_11_out, controlled_buffer_1_out[9], or_1_out);
  and and_12 (and_12_out, controlled_buffer_1_out[10], or_1_out);
  and and_13 (and_13_out, controlled_buffer_1_out[11], or_1_out);
  and and_14 (and_14_out, controlled_buffer_1_out[12], or_1_out);
  and and_15 (and_15_out, controlled_buffer_1_out[13], or_1_out);
  and and_16 (and_16_out, controlled_buffer_1_out[14], or_1_out);
  and and_17 (and_17_out, controlled_buffer_1_out[15], or_1_out);
  sram_1w word_1 (.wb_s(wb_s), .wordline(and_2_out), .R_or_W_b(and_18_out), .rb_s(rb_s));
  sram_1w word_2 (.wb_s(wb_s), .wordline(and_3_out), .R_or_W_b(and_18_out), .rb_s(rb_s));
  sram_1w word_3 (.wb_s(wb_s), .wordline(and_4_out), .R_or_W_b(and_18_out), .rb_s(rb_s));
  sram_1w word_4 (.wb_s(wb_s), .wordline(and_5_out), .R_or_W_b(and_18_out), .rb_s(rb_s));
  sram_1w word_5 (.wb_s(wb_s), .wordline(and_6_out), .R_or_W_b(and_18_out), .rb_s(rb_s));
  sram_1w word_6 (.wb_s(wb_s), .wordline(and_7_out), .R_or_W_b(and_18_out), .rb_s(rb_s));
  sram_1w word_7 (.wb_s(wb_s), .wordline(and_8_out), .R_or_W_b(and_18_out), .rb_s(rb_s));
  sram_1w word_8 (.wb_s(wb_s), .wordline(and_9_out), .R_or_W_b(and_18_out), .rb_s(rb_s));
  sram_1w word_9 (.wb_s(wb_s), .wordline(and_10_out), .R_or_W_b(and_18_out), .rb_s(rb_s));
  sram_1w word_10 (.wb_s(wb_s), .wordline(and_11_out), .R_or_W_b(and_18_out), .rb_s(rb_s));
  sram_1w word_11 (.wb_s(wb_s), .wordline(and_12_out), .R_or_W_b(and_18_out), .rb_s(rb_s));
  sram_1w word_12 (.wb_s(wb_s), .wordline(and_13_out), .R_or_W_b(and_18_out), .rb_s(rb_s));
  sram_1w word_13 (.wb_s(wb_s), .wordline(and_14_out), .R_or_W_b(and_18_out), .rb_s(rb_s));
  sram_1w word_14 (.wb_s(wb_s), .wordline(and_15_out), .R_or_W_b(and_18_out), .rb_s(rb_s));
  sram_1w word_15 (.wb_s(wb_s), .wordline(and_16_out), .R_or_W_b(and_18_out), .rb_s(rb_s));
  sram_1w word_16 (.wb_s(wb_s), .wordline(and_17_out), .R_or_W_b(and_18_out), .rb_s(rb_s));
  and and_18 (and_18_out, not_1_out, R_or_W_b);

  // Notes on the sheet:
  //   INIT: initial=0x1
endmodule

module sram_256w (
  input  [15:0] wb_s,
  input  INIT,
  input  addr_valid,
  input  R_or_W_b,
  input  CE,
  input  [7:0] addr8b_s,
  output [15:0] rb_s
);

  wire [15:0] dec_4to16_1_line_s;

  Dec_4to16 dec_4to16_1 (
    .b2(addr8b_s[6]), .b1(addr8b_s[5]), .b0(addr8b_s[4]), .EN(CE), .b3(addr8b_s[7]),
    .Line_s(dec_4to16_1_line_s));
  // NoConnect on dec_4to16_1_line_s[11]
  // NoConnect on dec_4to16_1_line_s[12]
  // NoConnect on dec_4to16_1_line_s[13]
  // NoConnect on dec_4to16_1_line_s[14]
  // NoConnect on dec_4to16_1_line_s[15]
  // NoConnect on dec_4to16_1_line_s[8]
  // NoConnect on dec_4to16_1_line_s[9]
  // NoConnect on dec_4to16_1_line_s[10]
  sram_16w M1 (
    .addr_valid(addr_valid), .addr4b_s(addr8b_s[3:0]), .CE(dec_4to16_1_line_s[0]), .wb_s(wb_s),
    .R_or_W_b(R_or_W_b), .INIT(INIT), .rb_s(rb_s));
  sram_16w M2 (
    .addr_valid(addr_valid), .addr4b_s(addr8b_s[3:0]), .CE(dec_4to16_1_line_s[1]), .wb_s(wb_s),
    .R_or_W_b(R_or_W_b), .INIT(INIT), .rb_s(rb_s));
  sram_16w M3 (
    .addr_valid(addr_valid), .addr4b_s(addr8b_s[3:0]), .CE(dec_4to16_1_line_s[2]), .wb_s(wb_s),
    .R_or_W_b(R_or_W_b), .INIT(INIT), .rb_s(rb_s));
  sram_16w M4 (
    .addr_valid(addr_valid), .addr4b_s(addr8b_s[3:0]), .CE(dec_4to16_1_line_s[3]), .wb_s(wb_s),
    .R_or_W_b(R_or_W_b), .INIT(INIT), .rb_s(rb_s));
  sram_16w M5 (
    .addr_valid(addr_valid), .addr4b_s(addr8b_s[3:0]), .CE(dec_4to16_1_line_s[4]), .wb_s(wb_s),
    .R_or_W_b(R_or_W_b), .INIT(INIT), .rb_s(rb_s));
  sram_16w M6 (
    .addr_valid(addr_valid), .addr4b_s(addr8b_s[3:0]), .CE(dec_4to16_1_line_s[5]), .wb_s(wb_s),
    .R_or_W_b(R_or_W_b), .INIT(INIT), .rb_s(rb_s));
  sram_16w M7 (
    .addr_valid(addr_valid), .addr4b_s(addr8b_s[3:0]), .CE(dec_4to16_1_line_s[6]), .wb_s(wb_s),
    .R_or_W_b(R_or_W_b), .INIT(INIT), .rb_s(rb_s));
  sram_16w M8 (
    .addr_valid(addr_valid), .addr4b_s(addr8b_s[3:0]), .CE(dec_4to16_1_line_s[7]), .wb_s(wb_s),
    .R_or_W_b(R_or_W_b), .INIT(INIT), .rb_s(rb_s));

  // Notes on the sheet:
  //   CE: initial=0x1
  //   addr_valid: initial=0x1
  //   INIT: initial=0x1
  //   256w is 16x16w
  //   address bus is 8bits deep
  //   only first 240 words are accessible; rest for I/O
endmodule

module regf_cell (
  input  RE,
  input  WE,
  input  wb,
  output rb
);

  wire and_1_out, and_2_out, controlled_inverter_2_out, not_1_out, not_2_out, not_3_out, not_4_out,
       not_6_out, not_7_out, not_8_out, transmission_1_p4, transmission_1_p5;

  and and_1 (and_1_out, WE, not_4_out);
  not not_1 (not_1_out, RE);
  // Transmission_Gate transmission_1: pin names not known; wires that end beside it: rb, not_1_out, RE, transmission_1_p4, transmission_1_p5
  not not_2 (not_2_out, and_1_out);
  not not_3 (not_3_out, and_1_out);
  not not_4 (not_4_out, wb);
  assign transmission_1_p4 = not_3_out ? ~controlled_inverter_2_out : 1'bz;  // Controlled_Inverter controlled_inverter_1
  not not_5 (transmission_1_p5, not_2_out);
  Transistor #(.\type ("n")) transistor_1 (.in(1'b0), .out(transmission_1_p4), .gate(transmission_1_p5));
  assign controlled_inverter_2_out = not_6_out ? ~transmission_1_p4 : 1'bz;  // Controlled_Inverter controlled_inverter_2
  not not_6 (not_6_out, and_2_out);
  and and_2 (and_2_out, WE, wb);
  not not_7 (not_7_out, and_2_out);
  Transistor #(.\type ("n")) transistor_2 (.in(1'b0), .out(controlled_inverter_2_out), .gate(not_8_out));
  not not_8 (not_8_out, not_7_out);

  // Notes on the sheet:
  //   ne se retrouve avec une entrée U pendant 1x delay !
  //   Ceci évite que un des 2 tampons inverseurs (haut ou bas selon le bit écrit) 
  //   tampon : 2x delay pour réactiver le feedback avant de couper la connection à la masse. 
endmodule

module regf_1w (
  input  wordline,
  input  [15:0] wb_s,
  input  WE,
  input  RE,
  output [15:0] rb_s
);

  wire and_1_out, and_2_out;

  and and_1 (and_1_out, wordline, WE);
  regf_cell regf_cell_1 (.RE(and_2_out), .WE(and_1_out), .wb(wb_s[15]), .rb(rb_s[15]));
  and and_2 (and_2_out, wordline, RE);
  regf_cell regf_cell_2 (.RE(and_2_out), .WE(and_1_out), .wb(wb_s[13]), .rb(rb_s[13]));
  regf_cell regf_cell_3 (.RE(and_2_out), .WE(and_1_out), .wb(wb_s[14]), .rb(rb_s[14]));
  regf_cell regf_cell_4 (.RE(and_2_out), .WE(and_1_out), .wb(wb_s[11]), .rb(rb_s[11]));
  regf_cell regf_cell_5 (.RE(and_2_out), .WE(and_1_out), .wb(wb_s[12]), .rb(rb_s[12]));
  regf_cell regf_cell_6 (.RE(and_2_out), .WE(and_1_out), .wb(wb_s[9]), .rb(rb_s[9]));
  regf_cell regf_cell_7 (.RE(and_2_out), .WE(and_1_out), .wb(wb_s[10]), .rb(rb_s[10]));
  regf_cell regf_cell_8 (.RE(and_2_out), .WE(and_1_out), .wb(wb_s[7]), .rb(rb_s[7]));
  regf_cell regf_cell_9 (.RE(and_2_out), .WE(and_1_out), .wb(wb_s[8]), .rb(rb_s[8]));
  regf_cell regf_cell_10 (.RE(and_2_out), .WE(and_1_out), .wb(wb_s[5]), .rb(rb_s[5]));
  regf_cell regf_cell_11 (.RE(and_2_out), .WE(and_1_out), .wb(wb_s[6]), .rb(rb_s[6]));
  regf_cell regf_cell_12 (.RE(and_2_out), .WE(and_1_out), .wb(wb_s[3]), .rb(rb_s[3]));
  regf_cell regf_cell_13 (.RE(and_2_out), .WE(and_1_out), .wb(wb_s[4]), .rb(rb_s[4]));
  regf_cell regf_cell_14 (.RE(and_2_out), .WE(and_1_out), .wb(wb_s[1]), .rb(rb_s[1]));
  regf_cell regf_cell_15 (.RE(and_2_out), .WE(and_1_out), .wb(wb_s[2]), .rb(rb_s[2]));
  regf_cell regf_cell_16 (.RE(and_2_out), .WE(and_1_out), .wb(wb_s[0]), .rb(rb_s[0]));
endmodule

module Dec_2to4 (
  input  b1,
  input  b0,
  input  EN,
  output [3:0] Line_s
);

  wire and_1_out, and_2_out, not_1_out, not_2_out;

  and and_1 (and_1_out, b1, EN);
  not not_1 (not_1_out, and_1_out);
  and and_2 (and_2_out, b0, EN);
  not not_2 (not_2_out, and_2_out);
  and L1 (Line_s[0], not_2_out, EN, not_1_out);
  and L2 (Line_s[1], and_2_out, not_1_out);
  and L3 (Line_s[2], not_2_out, and_1_out);
  and L4 (Line_s[3], and_2_out, and_1_out);
endmodule

module Dec_3to8 (
  input  b2,
  input  CE,
  input  b1,
  input  b0,
  output [7:0] Line_s
);

  wire and_1_out, and_2_out, not_1_out;

  not not_1 (not_1_out, b2);
  and and_1 (and_1_out, not_1_out, CE);
  Dec_2to4 dec_2to4_1 (.EN(and_1_out), .b1(b1), .b0(b0), .Line_s(Line_s[3:0]));
  and and_2 (and_2_out, b2, CE);
  Dec_2to4 dec_2to4_2 (.EN(and_2_out), .b1(b1), .b0(b0), .Line_s(Line_s[7:4]));

  // Notes on the sheet:
  //   0-3
  //   4-7
endmodule

module Mux_2w (
  input  sel,
  input  [15:0] In0,
  input  [15:0] In1,
  output [15:0] out_4
);

  wire buffer_1_out, not_1_out;
  wire [15:0] inverting_tristate_buffer_1bit_1_y;

  not not_1 (not_1_out, sel);
  buf buffer_1 (buffer_1_out, sel);
  inverting_tristate_buffer_1bit inverting_tristate_buffer_1bit_1 (
    .D(In0[0]), .OE(not_1_out), .Y(inverting_tristate_buffer_1bit_1_y[0]));
  inverting_tristate_buffer_1bit inverting_tristate_buffer_1bit_2 (
    .D(In0[1]), .OE(not_1_out), .Y(inverting_tristate_buffer_1bit_1_y[1]));
  inverting_tristate_buffer_1bit inverting_tristate_buffer_1bit_3 (
    .D(In0[2]), .OE(not_1_out), .Y(inverting_tristate_buffer_1bit_1_y[2]));
  inverting_tristate_buffer_1bit inverting_tristate_buffer_1bit_4 (
    .D(In0[3]), .OE(not_1_out), .Y(inverting_tristate_buffer_1bit_1_y[3]));
  inverting_tristate_buffer_1bit inverting_tristate_buffer_1bit_5 (
    .D(In0[4]), .OE(not_1_out), .Y(inverting_tristate_buffer_1bit_1_y[4]));
  inverting_tristate_buffer_1bit inverting_tristate_buffer_1bit_6 (
    .D(In0[5]), .OE(not_1_out), .Y(inverting_tristate_buffer_1bit_1_y[5]));
  inverting_tristate_buffer_1bit inverting_tristate_buffer_1bit_7 (
    .D(In0[6]), .OE(not_1_out), .Y(inverting_tristate_buffer_1bit_1_y[6]));
  inverting_tristate_buffer_1bit inverting_tristate_buffer_1bit_8 (
    .D(In0[7]), .OE(not_1_out), .Y(inverting_tristate_buffer_1bit_1_y[7]));
  inverting_tristate_buffer_1bit inverting_tristate_buffer_1bit_9 (
    .D(In0[8]), .OE(not_1_out), .Y(inverting_tristate_buffer_1bit_1_y[8]));
  inverting_tristate_buffer_1bit inverting_tristate_buffer_1bit_10 (
    .D(In0[9]), .OE(not_1_out), .Y(inverting_tristate_buffer_1bit_1_y[9]));
  inverting_tristate_buffer_1bit inverting_tristate_buffer_1bit_11 (
    .D(In0[10]), .OE(not_1_out), .Y(inverting_tristate_buffer_1bit_1_y[10]));
  inverting_tristate_buffer_1bit inverting_tristate_buffer_1bit_12 (
    .D(In0[11]), .OE(not_1_out), .Y(inverting_tristate_buffer_1bit_1_y[11]));
  inverting_tristate_buffer_1bit inverting_tristate_buffer_1bit_13 (
    .D(In0[12]), .OE(not_1_out), .Y(inverting_tristate_buffer_1bit_1_y[12]));
  inverting_tristate_buffer_1bit inverting_tristate_buffer_1bit_14 (
    .D(In0[13]), .OE(not_1_out), .Y(inverting_tristate_buffer_1bit_1_y[13]));
  inverting_tristate_buffer_1bit inverting_tristate_buffer_1bit_15 (
    .D(In0[14]), .OE(not_1_out), .Y(inverting_tristate_buffer_1bit_1_y[14]));
  inverting_tristate_buffer_1bit inverting_tristate_buffer_1bit_16 (
    .D(In0[15]), .OE(not_1_out), .Y(inverting_tristate_buffer_1bit_1_y[15]));
  inverting_tristate_buffer_1bit inverting_tristate_buffer_1bit_17 (
    .D(In1[0]), .OE(buffer_1_out), .Y(inverting_tristate_buffer_1bit_1_y[0]));
  inverting_tristate_buffer_1bit inverting_tristate_buffer_1bit_18 (
    .D(In1[1]), .OE(buffer_1_out), .Y(inverting_tristate_buffer_1bit_1_y[1]));
  inverting_tristate_buffer_1bit inverting_tristate_buffer_1bit_19 (
    .D(In1[2]), .OE(buffer_1_out), .Y(inverting_tristate_buffer_1bit_1_y[2]));
  inverting_tristate_buffer_1bit inverting_tristate_buffer_1bit_20 (
    .D(In1[3]), .OE(buffer_1_out), .Y(inverting_tristate_buffer_1bit_1_y[3]));
  inverting_tristate_buffer_1bit inverting_tristate_buffer_1bit_21 (
    .D(In1[4]), .OE(buffer_1_out), .Y(inverting_tristate_buffer_1bit_1_y[4]));
  inverting_tristate_buffer_1bit inverting_tristate_buffer_1bit_22 (
    .D(In1[5]), .OE(buffer_1_out), .Y(inverting_tristate_buffer_1bit_1_y[5]));
  inverting_tristate_buffer_1bit inverting_tristate_buffer_1bit_23 (
    .D(In1[6]), .OE(buffer_1_out), .Y(inverting_tristate_buffer_1bit_1_y[6]));
  inverting_tristate_buffer_1bit inverting_tristate_buffer_1bit_24 (
    .D(In1[7]), .OE(buffer_1_out), .Y(inverting_tristate_buffer_1bit_1_y[7]));
  inverting_tristate_buffer_1bit inverting_tristate_buffer_1bit_25 (
    .D(In1[8]), .OE(buffer_1_out), .Y(inverting_tristate_buffer_1bit_1_y[8]));
  inverting_tristate_buffer_1bit inverting_tristate_buffer_1bit_26 (
    .D(In1[9]), .OE(buffer_1_out), .Y(inverting_tristate_buffer_1bit_1_y[9]));
  inverting_tristate_buffer_1bit inverting_tristate_buffer_1bit_27 (
    .D(In1[10]), .OE(buffer_1_out), .Y(inverting_tristate_buffer_1bit_1_y[10]));
  inverting_tristate_buffer_1bit inverting_tristate_buffer_1bit_28 (
    .D(In1[11]), .OE(buffer_1_out), .Y(inverting_tristate_buffer_1bit_1_y[11]));
  inverting_tristate_buffer_1bit inverting_tristate_buffer_1bit_29 (
    .D(In1[12]), .OE(buffer_1_out), .Y(inverting_tristate_buffer_1bit_1_y[12]));
  inverting_tristate_buffer_1bit inverting_tristate_buffer_1bit_30 (
    .D(In1[13]), .OE(buffer_1_out), .Y(inverting_tristate_buffer_1bit_1_y[13]));
  inverting_tristate_buffer_1bit inverting_tristate_buffer_1bit_31 (
    .D(In1[14]), .OE(buffer_1_out), .Y(inverting_tristate_buffer_1bit_1_y[14]));
  inverting_tristate_buffer_1bit inverting_tristate_buffer_1bit_32 (
    .D(In1[15]), .OE(buffer_1_out), .Y(inverting_tristate_buffer_1bit_1_y[15]));
  assign out_4 = ~inverting_tristate_buffer_1bit_1_y;  // NOT_Gate not_2, 16 bits wide
endmodule

module alu_1bFA (
  input  a,
  input  b,
  input  cin,
  output s,
  output cout
);

  wire and_1_out, and_2_out, xor_1_out;

  xor xor_1 (xor_1_out, a, b);
  and and_1 (and_1_out, b, a);
  and and_2 (and_2_out, xor_1_out, cin);
  xor xor_2 (s, xor_1_out, cin);
  or or_1 (cout, and_2_out, and_1_out);

  // Notes on the sheet:
  //   1 bit Full Adder
  //   S = cin xor ( a xor b )
  //   cout = (a.b) or cin.(a xor b)
  //   a xor b
  //   a . b
  //    cin.(a xor b)
endmodule

module alu_4bFA (
  input  cin,
  input  [3:0] a,
  input  [3:0] b,
  output [3:0] s,
  output cout
);

  wire alu_1bfa_1_cout, alu_1bfa_2_cout, alu_1bfa_3_cout;

  alu_1bFA alu_1bfa_1 (.a(a[0]), .b(b[0]), .cin(cin), .s(s[0]), .cout(alu_1bfa_1_cout));
  alu_1bFA alu_1bfa_2 (.a(a[1]), .b(b[1]), .cin(alu_1bfa_1_cout), .s(s[1]), .cout(alu_1bfa_2_cout));
  alu_1bFA alu_1bfa_3 (.a(a[2]), .b(b[2]), .cin(alu_1bfa_2_cout), .s(s[2]), .cout(alu_1bfa_3_cout));
  alu_1bFA alu_1bfa_4 (.a(a[3]), .b(b[3]), .cin(alu_1bfa_3_cout), .s(s[3]), .cout(cout));
endmodule

module alu_16bAS (
  input  [15:0] a,
  input  [15:0] b,
  input  Sub_or_Add_b,
  output [15:0] S,
  output cout
);

  wire alu_4bfa_2_cout, alu_4bfa_3_cout, alu_4bfa_4_cout;
  wire [3:0] xor_1_out, xor_1_out_2, xor_1_out_3, xor_1_out_4;

  alu_4bFA alu_4bfa_1 (.cin(alu_4bfa_2_cout), .a(a[15:12]), .b(xor_1_out_4), .s(S[15:12]), .cout(cout));
  assign {xor_1_out_4, xor_1_out_3, xor_1_out_2, xor_1_out} = b ^ {16{Sub_or_Add_b}};  // XOR_Gate xor_1, 16 bits wide
  alu_4bFA alu_4bfa_2 (.cin(alu_4bfa_3_cout), .a(a[11:8]), .b(xor_1_out_3), .s(S[11:8]), .cout(alu_4bfa_2_cout));
  alu_4bFA alu_4bfa_3 (.cin(alu_4bfa_4_cout), .a(a[7:4]), .b(xor_1_out_2), .s(S[7:4]), .cout(alu_4bfa_3_cout));
  alu_4bFA alu_4bfa_4 (.cin(Sub_or_Add_b), .a(a[3:0]), .b(xor_1_out), .s(S[3:0]), .cout(alu_4bfa_4_cout));

  // Notes on the sheet:
  //   16 bits add / sub circuit 
  //   with ripple carry
endmodule

module alu_16bShifter (
  input  [15:0] a,
  input  shiftLL,
  input  shiftRA,
  input  shiftRL,
  output [15:0] Y
);

  TrisBuf_1w trisbuf_1w_1 (.D({a[14:0], 1'b0}), .OE(shiftLL), .Y(Y));
  TrisBuf_1w trisbuf_1w_2 (.D({{2{a[15]}}, a[14:1]}), .OE(shiftRA), .Y(Y));
  TrisBuf_1w trisbuf_1w_3 (.D({1'b0, a[15:1]}), .OE(shiftRL), .Y(Y));

  // Notes on the sheet:
  //   shift left, logical
  //   shift right, logical
  //   x2 operation, on signed or unsigned
  //   (provided no type overflow)
  //   shift right, arithmetical
  //   /2 operation, on signed ONLY
  //   /2 operation, on unsigned ONLY
endmodule

module alu_fullv1 (
  input  [3:0] ctrl,
  input  [15:0] A,
  input  [15:0] B,
  output [15:0] alu_out,
  output [3:0] alu_flags
);

  wire alu_16bas_1_cout, buffer_1_out, buffer_2_out, buffer_3_out, buffer_4_out, buffer_5_out, or_1_out,
       or_2_out, or_4_out;
  wire [7:0] or_3_out;
  wire [15:0] alu_16bas_1_s, alu_16bshifter_1_y, and_3_out, dec_4to16_1_line_s, or_5_out, xor_1_out;

  Dec_4to16 dec_4to16_1 (
    .b2(ctrl[2]), .b1(ctrl[1]), .b0(ctrl[0]), .EN(1'b1), .b3(ctrl[3]), .Line_s(dec_4to16_1_line_s));
  alu_16bAS alu_16bas_1 (
    .a(A), .b(B), .Sub_or_Add_b(dec_4to16_1_line_s[1]), .S(alu_16bas_1_s), .cout(alu_16bas_1_cout));
  or or_1 (or_1_out, dec_4to16_1_line_s[0], dec_4to16_1_line_s[1]);
  alu_16bShifter alu_16bshifter_1 (
    .a(A), .shiftLL(dec_4to16_1_line_s[5]), .shiftRA(dec_4to16_1_line_s[7]), .shiftRL(dec_4to16_1_line_s[6]),
    .Y(alu_16bshifter_1_y));
  or or_2 (or_2_out, dec_4to16_1_line_s[5], dec_4to16_1_line_s[6], dec_4to16_1_line_s[7]);
  TrisBuf_1w trisbuf_1w_1 (.D(alu_16bshifter_1_y), .OE(or_2_out), .Y({alu_flags[1], alu_out[14:0]}));
  TrisBuf_1w trisbuf_1w_2 (.D(alu_16bas_1_s), .OE(or_1_out), .Y({alu_flags[1], alu_out[14:0]}));
  // NoConnect on alu_out[14:0]
  TrisBuf_1w trisbuf_1w_3 (.D(and_3_out), .OE(buffer_1_out), .Y({alu_flags[1], alu_out[14:0]}));
  buf buffer_1 (buffer_1_out, dec_4to16_1_line_s[2]);
  TrisBuf_1w trisbuf_1w_4 (.D(or_5_out), .OE(buffer_2_out), .Y({alu_flags[1], alu_out[14:0]}));
  buf buffer_2 (buffer_2_out, dec_4to16_1_line_s[3]);
  TrisBuf_1w trisbuf_1w_5 (.D(xor_1_out), .OE(buffer_3_out), .Y({alu_flags[1], alu_out[14:0]}));
  buf buffer_3 (buffer_3_out, dec_4to16_1_line_s[4]);
  TrisBuf_1w trisbuf_1w_6 (.D({{8{1'b0}}, B[7:0]}), .OE(buffer_4_out), .Y({alu_flags[1], alu_out[14:0]}));
  buf buffer_4 (buffer_4_out, dec_4to16_1_line_s[8]);
  TrisBuf_1w trisbuf_1w_7 (.D({B[7:0], A[7:0]}), .OE(buffer_5_out), .Y({alu_flags[1], alu_out[14:0]}));
  buf buffer_5 (buffer_5_out, dec_4to16_1_line_s[9]);
  assign or_3_out = {alu_flags[1], alu_out[14:8]} | alu_out[7:0];  // OR_Gate or_3, 8 bits wide
  and and_1 (alu_flags[2], alu_flags[1], dec_4to16_1_line_s[1]);
  and and_2 (alu_flags[3], alu_16bas_1_cout, dec_4to16_1_line_s[0]);
  or or_4 (or_4_out, or_3_out[0], or_3_out[1], or_3_out[2], or_3_out[3], or_3_out[4], or_3_out[5], or_3_out[6], or_3_out[7]);
  assign and_3_out = A & B;  // AND_Gate and_3, 16 bits wide
  assign or_5_out = A | B;  // OR_Gate or_5, 16 bits wide
  assign xor_1_out = A ^ B;  // XOR_Gate xor_1, 16 bits wide
  not not_1 (alu_flags[0], or_4_out);

  assign alu_out[15] = alu_flags[1];

  // Notes on the sheet:
  //   add
  //   sub
  //   ctrls : add (A+B), sub (A-B), AND (A&B), OR (A|B), XOR (A^B), SLL_A (A<<1), SRL_A (A>>1), SRA_A (A>>>1), BLI&0U, BUI&AL
  //   or
  //   and
  //   SLL
  //   xor
  //   A < B ?
  //   SRL
  //   SRA
  //   BLI&AU
  //   BUI|AL
  //   CF | LTF | NF | ZF
endmodule

module program_counter_8b (
  input  sRst_b,
  input  COUNTEN,
  input  LOADEN,
  input  [7:0] L_s,
  input  clk,
  output [7:0] COUNTED,
  output ffOverflow
);

  wire and_1_out, bits_3_to_0_rcout, bits_7_to_4_rcout, buffer_1_out, buffer_2_out, buffer_3_out,
       buffer_4_out, buffer_5_out, buffer_6_out;

  buf buffer_1 (buffer_1_out, COUNTEN);
  buf buffer_2 (buffer_2_out, buffer_1_out);
  buf buffer_3 (buffer_3_out, LOADEN);
  buf buffer_4 (buffer_4_out, buffer_3_out);
  buf buffer_5 (buffer_5_out, buffer_6_out);
  buf buffer_6 (buffer_6_out, bits_3_to_0_rcout);
  and and_1 (and_1_out, buffer_2_out, buffer_5_out);
  program_counter_4b bits_7_to_4 (
    .COUNTEN(and_1_out), .L_s(L_s[7:4]), .LOADEN(buffer_4_out), .clk(clk), .sRst_b(sRst_b),
    .cOut_s(COUNTED[7:4]), .rcOut(bits_7_to_4_rcout));
  and and_2 (ffOverflow, bits_7_to_4_rcout, bits_3_to_0_rcout);
  program_counter_4b bits_3_to_0 (
    .COUNTEN(buffer_2_out), .L_s(L_s[3:0]), .LOADEN(buffer_4_out), .clk(clk), .sRst_b(sRst_b),
    .cOut_s(COUNTED[3:0]), .rcOut(bits_3_to_0_rcout));
endmodule

module Dff_16b (
  input  sRst_b,
  input  EN,
  input  clk,
  input  [15:0] D_16,
  output [15:0] Q_16
);

  wire buffer_1_out, buffer_2_out, or_1_out;

  buf buffer_1 (buffer_1_out, or_1_out);
  buf buffer_2 (buffer_2_out, buffer_1_out);
  or or_1 (or_1_out, ~sRst_b, EN);  // OR_Gate
  D_flipflop_sClr_en d_flipflop_sclr_en_1 (
    .D(D_16[0]), .en(buffer_2_out), .clk(clk), .CLR(sRst_b), .Q(Q_16[0]));  // open: Q_b
  D_flipflop_sClr_en d_flipflop_sclr_en_2 (
    .D(D_16[2]), .en(buffer_2_out), .clk(clk), .CLR(sRst_b), .Q(Q_16[2]));  // open: Q_b
  D_flipflop_sClr_en d_flipflop_sclr_en_3 (
    .D(D_16[4]), .en(buffer_2_out), .clk(clk), .CLR(sRst_b), .Q(Q_16[4]));  // open: Q_b
  D_flipflop_sClr_en d_flipflop_sclr_en_4 (
    .D(D_16[6]), .en(buffer_2_out), .clk(clk), .CLR(sRst_b), .Q(Q_16[6]));  // open: Q_b
  D_flipflop_sClr_en d_flipflop_sclr_en_5 (
    .D(D_16[8]), .en(buffer_2_out), .clk(clk), .CLR(sRst_b), .Q(Q_16[8]));  // open: Q_b
  D_flipflop_sClr_en d_flipflop_sclr_en_6 (
    .D(D_16[10]), .en(buffer_2_out), .clk(clk), .CLR(sRst_b), .Q(Q_16[10]));  // open: Q_b
  D_flipflop_sClr_en d_flipflop_sclr_en_7 (
    .D(D_16[12]), .en(buffer_2_out), .clk(clk), .CLR(sRst_b), .Q(Q_16[12]));  // open: Q_b
  D_flipflop_sClr_en d_flipflop_sclr_en_8 (
    .D(D_16[14]), .en(buffer_2_out), .clk(clk), .CLR(sRst_b), .Q(Q_16[14]));  // open: Q_b
  D_flipflop_sClr_en d_flipflop_sclr_en_9 (
    .D(D_16[1]), .en(buffer_2_out), .clk(clk), .CLR(sRst_b), .Q(Q_16[1]));  // open: Q_b
  D_flipflop_sClr_en d_flipflop_sclr_en_10 (
    .D(D_16[3]), .en(buffer_2_out), .clk(clk), .CLR(sRst_b), .Q(Q_16[3]));  // open: Q_b
  D_flipflop_sClr_en d_flipflop_sclr_en_11 (
    .D(D_16[5]), .en(buffer_2_out), .clk(clk), .CLR(sRst_b), .Q(Q_16[5]));  // open: Q_b
  D_flipflop_sClr_en d_flipflop_sclr_en_12 (
    .D(D_16[7]), .en(buffer_2_out), .clk(clk), .CLR(sRst_b), .Q(Q_16[7]));  // open: Q_b
  D_flipflop_sClr_en d_flipflop_sclr_en_13 (
    .D(D_16[9]), .en(buffer_2_out), .clk(clk), .CLR(sRst_b), .Q(Q_16[9]));  // open: Q_b
  D_flipflop_sClr_en d_flipflop_sclr_en_14 (
    .D(D_16[11]), .en(buffer_2_out), .clk(clk), .CLR(sRst_b), .Q(Q_16[11]));  // open: Q_b
  D_flipflop_sClr_en d_flipflop_sclr_en_15 (
    .D(D_16[13]), .en(buffer_2_out), .clk(clk), .CLR(sRst_b), .Q(Q_16[13]));  // open: Q_b
  D_flipflop_sClr_en d_flipflop_sclr_en_16 (
    .D(D_16[15]), .en(buffer_2_out), .clk(clk), .CLR(sRst_b), .Q(Q_16[15]));  // open: Q_b

  // Notes on the sheet:
  //   EN: initial=0x1
  //   little bit of delay because EN 1=>0 when clk posedge
  //   RESET : sRst_b = 0 , EN =1, 1 tick
endmodule

module regf_cell_Dual (
  input  re1,
  input  re2,
  input  WE,
  input  wb,
  output rb1,
  output rb2
);

  wire controlled_inverter_1_out, controlled_inverter_2_out, nand_1_out, not_1_out, not_2_out, or_1_out;

  assign rb1 = re1 ? controlled_inverter_1_out : 1'bz;  // Controlled_Buffer controlled_buffer_1
  or or_1 (or_1_out, ~WE, wb);  // OR_Gate
  assign controlled_inverter_1_out = or_1_out ? ~controlled_inverter_2_out : 1'bz;  // Controlled_Inverter controlled_inverter_1
  not not_1 (not_1_out, or_1_out);
  Transistor #(.\type ("n")) transistor_1 (.in(1'b0), .out(controlled_inverter_1_out), .gate(not_1_out));
  assign controlled_inverter_2_out = nand_1_out ? ~controlled_inverter_1_out : 1'bz;  // Controlled_Inverter controlled_inverter_2
  nand nand_1 (nand_1_out, WE, wb);
  not not_2 (not_2_out, nand_1_out);
  Transistor #(.\type ("n")) transistor_2 (.in(1'b0), .out(controlled_inverter_2_out), .gate(not_2_out));
  assign rb2 = re2 ? ~controlled_inverter_2_out : 1'bz;  // Controlled_Inverter controlled_inverter_3

  // Notes on the sheet:
  //   ne se retrouve avec une entrée U pendant 1x delay !
  //   Ceci évite que un des 2 tampons inverseurs (haut ou bas selon le bit écrit) 
  //   tampon : 2x delay pour réactiver le feedback avant de couper la connection à la masse. 
endmodule

module regf_1w_Dual (
  input  [15:0] wb_s,
  input  WE,
  input  RE1,
  input  RE2,
  output [15:0] rb1_s,
  output [15:0] rb2_s
);

  regf_cell_Dual regf_cell_dual_1 (.re1(RE1), .WE(WE), .wb(wb_s[15]), .re2(RE2), .rb1(rb1_s[15]), .rb2(rb2_s[15]));
  regf_cell_Dual regf_cell_dual_2 (.re1(RE1), .WE(WE), .wb(wb_s[14]), .re2(RE2), .rb1(rb1_s[14]), .rb2(rb2_s[14]));
  regf_cell_Dual regf_cell_dual_3 (.re1(RE1), .WE(WE), .wb(wb_s[13]), .re2(RE2), .rb1(rb1_s[13]), .rb2(rb2_s[13]));
  regf_cell_Dual regf_cell_dual_4 (.re1(RE1), .WE(WE), .wb(wb_s[11]), .re2(RE2), .rb1(rb1_s[11]), .rb2(rb2_s[11]));
  regf_cell_Dual regf_cell_dual_5 (.re1(RE1), .WE(WE), .wb(wb_s[12]), .re2(RE2), .rb1(rb1_s[12]), .rb2(rb2_s[12]));
  regf_cell_Dual regf_cell_dual_6 (.re1(RE1), .WE(WE), .wb(wb_s[10]), .re2(RE2), .rb1(rb1_s[10]), .rb2(rb2_s[10]));
  regf_cell_Dual regf_cell_dual_7 (.re1(RE1), .WE(WE), .wb(wb_s[9]), .re2(RE2), .rb1(rb1_s[9]), .rb2(rb2_s[9]));
  regf_cell_Dual regf_cell_dual_8 (.re1(RE1), .WE(WE), .wb(wb_s[8]), .re2(RE2), .rb1(rb1_s[8]), .rb2(rb2_s[8]));
  regf_cell_Dual regf_cell_dual_9 (.re1(RE1), .WE(WE), .wb(wb_s[7]), .re2(RE2), .rb1(rb1_s[7]), .rb2(rb2_s[7]));
  regf_cell_Dual regf_cell_dual_10 (.re1(RE1), .WE(WE), .wb(wb_s[6]), .re2(RE2), .rb1(rb1_s[6]), .rb2(rb2_s[6]));
  regf_cell_Dual regf_cell_dual_11 (.re1(RE1), .WE(WE), .wb(wb_s[5]), .re2(RE2), .rb1(rb1_s[5]), .rb2(rb2_s[5]));
  regf_cell_Dual regf_cell_dual_12 (.re1(RE1), .WE(WE), .wb(wb_s[3]), .re2(RE2), .rb1(rb1_s[3]), .rb2(rb2_s[3]));
  regf_cell_Dual regf_cell_dual_13 (.re1(RE1), .WE(WE), .wb(wb_s[4]), .re2(RE2), .rb1(rb1_s[4]), .rb2(rb2_s[4]));
  regf_cell_Dual regf_cell_dual_14 (.re1(RE1), .WE(WE), .wb(wb_s[2]), .re2(RE2), .rb1(rb1_s[2]), .rb2(rb2_s[2]));
  regf_cell_Dual regf_cell_dual_15 (.re1(RE1), .WE(WE), .wb(wb_s[1]), .re2(RE2), .rb1(rb1_s[1]), .rb2(rb2_s[1]));
  regf_cell_Dual regf_cell_dual_16 (.re1(RE1), .WE(WE), .wb(wb_s[0]), .re2(RE2), .rb1(rb1_s[0]), .rb2(rb2_s[0]));
endmodule

module Dff_4b (
  input  sRst_b,
  input  clk,
  input  EN,
  input  [3:0] D_4,
  output [3:0] Q_4
);

  wire d_flipflop_sclr_en_1_q_b, d_flipflop_sclr_en_2_q_b, d_flipflop_sclr_en_3_q_b, d_flipflop_sclr_en_4_q_b;

  D_flipflop_sClr_en d_flipflop_sclr_en_1 (
    .D(D_4[0]), .en(EN), .clk(clk), .CLR(sRst_b), .Q(Q_4[0]), .Q_b(d_flipflop_sclr_en_1_q_b));
  // NoConnect on d_flipflop_sclr_en_1_q_b
  D_flipflop_sClr_en d_flipflop_sclr_en_2 (
    .D(D_4[2]), .en(EN), .clk(clk), .CLR(sRst_b), .Q(Q_4[2]), .Q_b(d_flipflop_sclr_en_2_q_b));
  // NoConnect on d_flipflop_sclr_en_2_q_b
  D_flipflop_sClr_en d_flipflop_sclr_en_3 (
    .D(D_4[1]), .en(EN), .clk(clk), .CLR(sRst_b), .Q(Q_4[1]), .Q_b(d_flipflop_sclr_en_3_q_b));
  // NoConnect on d_flipflop_sclr_en_3_q_b
  D_flipflop_sClr_en d_flipflop_sclr_en_4 (
    .D(D_4[3]), .en(EN), .clk(clk), .CLR(sRst_b), .Q(Q_4[3]), .Q_b(d_flipflop_sclr_en_4_q_b));
  // NoConnect on d_flipflop_sclr_en_4_q_b

  // Notes on the sheet:
  //   EN: initial=0x1
endmodule

module regf_s0 (
  input  RE1,
  input  RE2,
  output [15:0] rb1_s,
  output [15:0] rb2_s
);

  TrisBuf_1w trisbuf_1w_1 (.D({16{1'b0}}), .OE(RE1), .Y(rb1_s));
  TrisBuf_1w trisbuf_1w_2 (.D({16{1'b0}}), .OE(RE2), .Y(rb2_s));
endmodule

module D_latch_3b (
  input  [2:0] D,
  input  sClr_b,
  input  EN,
  output [2:0] Q
);

  wire d_latch_sclr_1_q_b, d_latch_sclr_2_q_b, d_latch_sclr_3_q_b, or_1_out;

  or or_1 (or_1_out, ~sClr_b, EN);  // OR_Gate
  D_latch_sClr d_latch_sclr_1 (.D(D[2]), .sCLR_b(sClr_b), .EN(or_1_out), .Q(Q[2]), .Q_b(d_latch_sclr_1_q_b));
  // NoConnect on d_latch_sclr_1_q_b
  D_latch_sClr d_latch_sclr_2 (.D(D[1]), .sCLR_b(sClr_b), .EN(or_1_out), .Q(Q[1]), .Q_b(d_latch_sclr_2_q_b));
  // NoConnect on d_latch_sclr_2_q_b
  D_latch_sClr d_latch_sclr_3 (.D(D[0]), .sCLR_b(sClr_b), .EN(or_1_out), .Q(Q[0]), .Q_b(d_latch_sclr_3_q_b));
  // NoConnect on d_latch_sclr_3_q_b
endmodule

module D_latch_16b (
  input  [15:0] D,
  input  sClr_b,
  input  EN,
  output [15:0] Q
);

  wire d_latch_sclr_1_q_b, d_latch_sclr_2_q_b, d_latch_sclr_3_q_b, d_latch_sclr_4_q_b, d_latch_sclr_5_q_b,
       d_latch_sclr_6_q_b, d_latch_sclr_7_q_b, d_latch_sclr_8_q_b, d_latch_sclr_9_q_b, d_latch_sclr_10_q_b,
       d_latch_sclr_11_q_b, d_latch_sclr_12_q_b, d_latch_sclr_13_q_b, d_latch_sclr_14_q_b,
       d_latch_sclr_15_q_b, d_latch_sclr_16_q_b, or_1_out;

  or or_1 (or_1_out, ~sClr_b, EN);  // OR_Gate
  D_latch_sClr d_latch_sclr_1 (.D(D[15]), .sCLR_b(sClr_b), .EN(or_1_out), .Q(Q[15]), .Q_b(d_latch_sclr_1_q_b));
  // NoConnect on d_latch_sclr_1_q_b
  D_latch_sClr d_latch_sclr_2 (.D(D[14]), .sCLR_b(sClr_b), .EN(or_1_out), .Q(Q[14]), .Q_b(d_latch_sclr_2_q_b));
  // NoConnect on d_latch_sclr_2_q_b
  D_latch_sClr d_latch_sclr_3 (.D(D[13]), .sCLR_b(sClr_b), .EN(or_1_out), .Q(Q[13]), .Q_b(d_latch_sclr_3_q_b));
  D_latch_sClr d_latch_sclr_4 (.D(D[12]), .sCLR_b(sClr_b), .EN(or_1_out), .Q(Q[12]), .Q_b(d_latch_sclr_4_q_b));
  // NoConnect on d_latch_sclr_3_q_b
  D_latch_sClr d_latch_sclr_5 (.D(D[11]), .sCLR_b(sClr_b), .EN(or_1_out), .Q(Q[11]), .Q_b(d_latch_sclr_5_q_b));
  // NoConnect on d_latch_sclr_4_q_b
  // NoConnect on d_latch_sclr_5_q_b
  D_latch_sClr d_latch_sclr_6 (.D(D[10]), .sCLR_b(sClr_b), .EN(or_1_out), .Q(Q[10]), .Q_b(d_latch_sclr_6_q_b));
  // NoConnect on d_latch_sclr_6_q_b
  D_latch_sClr d_latch_sclr_7 (.D(D[9]), .sCLR_b(sClr_b), .EN(or_1_out), .Q(Q[9]), .Q_b(d_latch_sclr_7_q_b));
  D_latch_sClr d_latch_sclr_8 (.D(D[8]), .sCLR_b(sClr_b), .EN(or_1_out), .Q(Q[8]), .Q_b(d_latch_sclr_8_q_b));
  // NoConnect on d_latch_sclr_7_q_b
  D_latch_sClr d_latch_sclr_9 (.D(D[7]), .sCLR_b(sClr_b), .EN(or_1_out), .Q(Q[7]), .Q_b(d_latch_sclr_9_q_b));
  // NoConnect on d_latch_sclr_8_q_b
  // NoConnect on d_latch_sclr_9_q_b
  D_latch_sClr d_latch_sclr_10 (.D(D[6]), .sCLR_b(sClr_b), .EN(or_1_out), .Q(Q[6]), .Q_b(d_latch_sclr_10_q_b));
  // NoConnect on d_latch_sclr_10_q_b
  D_latch_sClr d_latch_sclr_11 (.D(D[5]), .sCLR_b(sClr_b), .EN(or_1_out), .Q(Q[5]), .Q_b(d_latch_sclr_11_q_b));
  D_latch_sClr d_latch_sclr_12 (.D(D[4]), .sCLR_b(sClr_b), .EN(or_1_out), .Q(Q[4]), .Q_b(d_latch_sclr_12_q_b));
  // NoConnect on d_latch_sclr_11_q_b
  D_latch_sClr d_latch_sclr_13 (.D(D[3]), .sCLR_b(sClr_b), .EN(or_1_out), .Q(Q[3]), .Q_b(d_latch_sclr_13_q_b));
  // NoConnect on d_latch_sclr_13_q_b
  // NoConnect on d_latch_sclr_12_q_b
  D_latch_sClr d_latch_sclr_14 (.D(D[2]), .sCLR_b(sClr_b), .EN(or_1_out), .Q(Q[2]), .Q_b(d_latch_sclr_14_q_b));
  // NoConnect on d_latch_sclr_14_q_b
  D_latch_sClr d_latch_sclr_15 (.D(D[1]), .sCLR_b(sClr_b), .EN(or_1_out), .Q(Q[1]), .Q_b(d_latch_sclr_15_q_b));
  D_latch_sClr d_latch_sclr_16 (.D(D[0]), .sCLR_b(sClr_b), .EN(or_1_out), .Q(Q[0]), .Q_b(d_latch_sclr_16_q_b));
  // NoConnect on d_latch_sclr_15_q_b
  // NoConnect on d_latch_sclr_16_q_b
endmodule

module ramx2_with_prog (
  input  R_or_W_b,
  input  INIT,
  input  [15:0] wb_s,
  input  [7:0] addr_s,
  input  PROG,
  input  clk,
  output [15:0] rb_s,
  output beingProged
);

  wire and_1_out, and_3_out, and_4_out, and_5_out, and_6_out, buffer_3_out, jk_flipflop_v2_1_q_b, not_1_out,
       not_2_out, not_3_out, not_4_out, or_1_out, program_counter_8b_1_ffoverflow;
  wire [6:2] undriven;
  wire [7:0] controlled_buffer_1_out, program_counter_8b_1_counted;
  wire [7:3] undriven_2;
  wire [15:0] buffer_1_out, buffer_2_out, controlled_buffer_3_out, rom_1_data;

  and and_1 (and_1_out, INIT, PROG, jk_flipflop_v2_1_q_b);
  not not_1 (not_1_out, INIT);
  and and_2 (beingProged, PROG, jk_flipflop_v2_1_q_b);
  not not_2 (not_2_out, clk);
  and and_3 (and_3_out, ~PROG, R_or_W_b, ~INIT);  // AND_Gate
  assign controlled_buffer_1_out = buffer_3_out ? program_counter_8b_1_counted : 8'bz;  // Controlled_Buffer controlled_buffer_1
  program_counter_8b program_counter_8b_1 (
    .clk(clk), .COUNTEN(beingProged), .LOADEN(INIT), .L_s({8{1'b0}}), .sRst_b(not_1_out),
    .ffOverflow(program_counter_8b_1_ffoverflow), .COUNTED(program_counter_8b_1_counted));
  sram_256w sram_256w_1 (
    .addr8b_s(controlled_buffer_1_out), .CE(not_4_out), .addr_valid(not_2_out), .wb_s(buffer_1_out),
    .INIT(and_1_out), .R_or_W_b(and_3_out), .rb_s(rb_s));
  assign buffer_1_out = buffer_2_out;  // Buffer buffer_1, 16 bits wide
  assign buffer_2_out = controlled_buffer_3_out;  // Buffer buffer_2, 16 bits wide
  assign controlled_buffer_1_out = not_3_out ? addr_s : 8'bz;  // Controlled_Buffer controlled_buffer_2
  ROM #(.dataWidth(16)) rom_1 (.addr(program_counter_8b_1_counted), .data(rom_1_data));
  jk_flipflop_V2 jk_flipflop_v2_1 (
    .J(program_counter_8b_1_ffoverflow), .K(program_counter_8b_1_ffoverflow), .clk(clk), .sRst_b(not_1_out),
    .Q_b(jk_flipflop_v2_1_q_b));  // open: Q
  or or_1 (or_1_out, PROG, INIT);
  buf buffer_3 (buffer_3_out, or_1_out);
  assign controlled_buffer_3_out = buffer_3_out ? rom_1_data : 16'bz;  // Controlled_Buffer controlled_buffer_3
  not not_3 (not_3_out, or_1_out);
  assign controlled_buffer_3_out = not_3_out ? wb_s : 16'bz;  // Controlled_Buffer controlled_buffer_4
  and and_4 (and_4_out, undriven_2[3], undriven[2]);
  and and_5 (and_5_out, undriven_2[5], undriven[4]);
  and and_6 (and_6_out, undriven_2[7], undriven[6]);
  not not_4 (not_4_out, addr_s[7]);
  // NAND_Gate nand_1 has open pins: in0=and_4_out, in1=and_5_out, in2=and_6_out, out=open

  // Notes on the sheet:
  //   INIT: initial=0x1
  //   addr_s: initial=0xf0
  //   cst '1 here to verify by read
  //   only 128 fisrt addresses supported
  //   contents of rom_1 (hex, n*v repeats v):
  //   0 d409 d508 580 e240 4 e280 1 d77c 6814 eed 6007 620 6002 600 2591 2a55 6ff1 cf20 7006 cfc0 6000
  //   once proged, can't be run again without a new INIT
  //   rb_s != 'U if clk on low phase and CS
  //   CS
endmodule

module sram_1wOpt (
  input  [15:0] wb_s,
  input  wordline,
  input  R_Wb,
  output [15:0] rb_s
);

  wire not_1_out, RE_out, WE_b_out;
  wire [15:0] buffer_1_out, controlled_inverter_1_out, not_5_out, not_18_out;

  not not_1 (not_1_out, WE_b_out);
  or WE_b (WE_b_out, ~wordline, R_Wb);  // OR_Gate
  and RE (RE_out, wordline, R_Wb);
  assign controlled_inverter_1_out = not_1_out ? ~buffer_1_out : 16'bz;  // Controlled_Inverter controlled_inverter_1
  not not_2 (not_18_out[15], controlled_inverter_1_out[15]);
  assign controlled_inverter_1_out[15] = WE_b_out ? ~not_18_out[15] : 1'bz;  // Controlled_Inverter controlled_inverter_2
  assign controlled_inverter_1_out[14] = WE_b_out ? ~not_18_out[14] : 1'bz;  // Controlled_Inverter controlled_inverter_3
  assign buffer_1_out = not_5_out;  // Buffer buffer_1, 16 bits wide
  not not_3 (not_18_out[13], controlled_inverter_1_out[13]);
  assign controlled_inverter_1_out[13] = WE_b_out ? ~not_18_out[13] : 1'bz;  // Controlled_Inverter controlled_inverter_4
  not not_4 (not_18_out[14], controlled_inverter_1_out[14]);
  assign controlled_inverter_1_out[12] = WE_b_out ? ~not_18_out[12] : 1'bz;  // Controlled_Inverter controlled_inverter_5
  assign not_5_out = ~wb_s;  // NOT_Gate not_5, 16 bits wide
  assign controlled_inverter_1_out[11] = WE_b_out ? ~not_18_out[11] : 1'bz;  // Controlled_Inverter controlled_inverter_6
  not not_6 (not_18_out[12], controlled_inverter_1_out[12]);
  not not_7 (not_18_out[11], controlled_inverter_1_out[11]);
  assign controlled_inverter_1_out[9] = WE_b_out ? ~not_18_out[9] : 1'bz;  // Controlled_Inverter controlled_inverter_7
  not not_8 (not_18_out[10], controlled_inverter_1_out[10]);
  assign controlled_inverter_1_out[10] = WE_b_out ? ~not_18_out[10] : 1'bz;  // Controlled_Inverter controlled_inverter_8
  not not_9 (not_18_out[9], controlled_inverter_1_out[9]);
  not not_10 (not_18_out[8], controlled_inverter_1_out[8]);
  assign controlled_inverter_1_out[8] = WE_b_out ? ~not_18_out[8] : 1'bz;  // Controlled_Inverter controlled_inverter_9
  not not_11 (not_18_out[7], controlled_inverter_1_out[7]);
  assign controlled_inverter_1_out[7] = WE_b_out ? ~not_18_out[7] : 1'bz;  // Controlled_Inverter controlled_inverter_10
  assign controlled_inverter_1_out[6] = WE_b_out ? ~not_18_out[6] : 1'bz;  // Controlled_Inverter controlled_inverter_11
  assign rb_s = RE_out ? ~not_18_out : 16'bz;  // Controlled_Inverter controlled_inverter_12
  not not_12 (not_18_out[5], controlled_inverter_1_out[5]);
  assign controlled_inverter_1_out[5] = WE_b_out ? ~not_18_out[5] : 1'bz;  // Controlled_Inverter controlled_inverter_13
  not not_13 (not_18_out[6], controlled_inverter_1_out[6]);
  assign controlled_inverter_1_out[4] = WE_b_out ? ~not_18_out[4] : 1'bz;  // Controlled_Inverter controlled_inverter_14
  assign controlled_inverter_1_out[3] = WE_b_out ? ~not_18_out[3] : 1'bz;  // Controlled_Inverter controlled_inverter_15
  not not_14 (not_18_out[4], controlled_inverter_1_out[4]);
  not not_15 (not_18_out[3], controlled_inverter_1_out[3]);
  assign controlled_inverter_1_out[1] = WE_b_out ? ~not_18_out[1] : 1'bz;  // Controlled_Inverter controlled_inverter_16
  not not_16 (not_18_out[2], controlled_inverter_1_out[2]);
  assign controlled_inverter_1_out[2] = WE_b_out ? ~not_18_out[2] : 1'bz;  // Controlled_Inverter controlled_inverter_17
  not not_17 (not_18_out[1], controlled_inverter_1_out[1]);
  not not_18 (not_18_out[0], controlled_inverter_1_out[0]);
  assign controlled_inverter_1_out[0] = WE_b_out ? ~not_18_out[0] : 1'bz;  // Controlled_Inverter controlled_inverter_18

  // Notes on the sheet:
  //   wordline: initial=0x1
  //   retard pour reactiver les 16 retroactions avant de couper l'alim sur stored.
  //   stored
  //   15
  //   !stored
  //   14
  //   13
  //   11
  //   12
  //   10
  //   wb_s is latched and overlaps on next half-clk to ensure wb_s hasnt changed by the time each cell locks on (from !we=0->1)
  //   9
  //   8
  //   7
  //   6
  //   5
  //   3
  //   4
  //   2
  //   1
  //   0
endmodule

module sram_16wOpt (
  input  [15:0] wb_s,
  input  R_Wb,
  input  CE,
  input  addr_valid,
  input  [3:0] addr4b_s,
  output [15:0] rb_s
);

  wire and_1_out;
  wire [15:0] dec_4to16_1_line_s;

  and and_1 (and_1_out, CE, addr_valid);
  Dec_4to16 dec_4to16_1 (
    .b2(addr4b_s[2]), .b1(addr4b_s[1]), .b0(addr4b_s[0]), .EN(and_1_out), .b3(addr4b_s[3]),
    .Line_s(dec_4to16_1_line_s));
  sram_1wOpt word_0 (.wordline(dec_4to16_1_line_s[0]), .wb_s(wb_s), .R_Wb(R_Wb), .rb_s(rb_s));
  sram_1wOpt word_1 (.wordline(dec_4to16_1_line_s[1]), .wb_s(wb_s), .R_Wb(R_Wb), .rb_s(rb_s));
  sram_1wOpt word_2 (.wordline(dec_4to16_1_line_s[2]), .wb_s(wb_s), .R_Wb(R_Wb), .rb_s(rb_s));
  sram_1wOpt word_3 (.wordline(dec_4to16_1_line_s[3]), .wb_s(wb_s), .R_Wb(R_Wb), .rb_s(rb_s));
  sram_1wOpt word_4 (.wordline(dec_4to16_1_line_s[4]), .wb_s(wb_s), .R_Wb(R_Wb), .rb_s(rb_s));
  sram_1wOpt word_5 (.wordline(dec_4to16_1_line_s[5]), .wb_s(wb_s), .R_Wb(R_Wb), .rb_s(rb_s));
  sram_1wOpt word_6 (.wordline(dec_4to16_1_line_s[6]), .wb_s(wb_s), .R_Wb(R_Wb), .rb_s(rb_s));
  sram_1wOpt word_7 (.wordline(dec_4to16_1_line_s[7]), .wb_s(wb_s), .R_Wb(R_Wb), .rb_s(rb_s));
  sram_1wOpt word_8 (.wordline(dec_4to16_1_line_s[8]), .wb_s(wb_s), .R_Wb(R_Wb), .rb_s(rb_s));
  sram_1wOpt word_9 (.wordline(dec_4to16_1_line_s[9]), .wb_s(wb_s), .R_Wb(R_Wb), .rb_s(rb_s));
  sram_1wOpt word_10 (.wordline(dec_4to16_1_line_s[10]), .wb_s(wb_s), .R_Wb(R_Wb), .rb_s(rb_s));
  sram_1wOpt word_11 (.wordline(dec_4to16_1_line_s[11]), .wb_s(wb_s), .R_Wb(R_Wb), .rb_s(rb_s));
  sram_1wOpt word_12 (.wordline(dec_4to16_1_line_s[12]), .wb_s(wb_s), .R_Wb(R_Wb), .rb_s(rb_s));
  sram_1wOpt word_13 (.wordline(dec_4to16_1_line_s[13]), .wb_s(wb_s), .R_Wb(R_Wb), .rb_s(rb_s));
  sram_1wOpt word_14 (.wordline(dec_4to16_1_line_s[14]), .wb_s(wb_s), .R_Wb(R_Wb), .rb_s(rb_s));
  sram_1wOpt word_15 (.wordline(dec_4to16_1_line_s[15]), .wb_s(wb_s), .R_Wb(R_Wb), .rb_s(rb_s));
endmodule

module sram_128wOpt (
  input  [15:0] wb_s,
  input  addr_valid,
  input  R_Wb,
  input  CE,
  input  [7:0] addr8b_s,
  output [15:0] rb_s
);

  wire [7:0] dec_3to8_1_line_s;

  // NoConnect on addr8b_s[7]
  Dec_3to8 dec_3to8_1 (.b2(addr8b_s[6]), .b1(addr8b_s[5]), .b0(addr8b_s[4]), .CE(CE), .Line_s(dec_3to8_1_line_s));
  sram_16wOpt sram_16wopt_1 (
    .addr_valid(addr_valid), .addr4b_s(addr8b_s[3:0]), .wb_s(wb_s), .R_Wb(R_Wb), .CE(dec_3to8_1_line_s[0]),
    .rb_s(rb_s));
  sram_16wOpt sram_16wopt_2 (
    .addr_valid(addr_valid), .addr4b_s(addr8b_s[3:0]), .wb_s(wb_s), .R_Wb(R_Wb), .CE(dec_3to8_1_line_s[1]),
    .rb_s(rb_s));
  sram_16wOpt sram_16wopt_3 (
    .addr_valid(addr_valid), .addr4b_s(addr8b_s[3:0]), .wb_s(wb_s), .R_Wb(R_Wb), .CE(dec_3to8_1_line_s[2]),
    .rb_s(rb_s));
  sram_16wOpt sram_16wopt_4 (
    .addr_valid(addr_valid), .addr4b_s(addr8b_s[3:0]), .wb_s(wb_s), .R_Wb(R_Wb), .CE(dec_3to8_1_line_s[3]),
    .rb_s(rb_s));
  sram_16wOpt sram_16wopt_5 (
    .addr_valid(addr_valid), .addr4b_s(addr8b_s[3:0]), .wb_s(wb_s), .R_Wb(R_Wb), .CE(dec_3to8_1_line_s[4]),
    .rb_s(rb_s));
  sram_16wOpt sram_16wopt_6 (
    .addr_valid(addr_valid), .addr4b_s(addr8b_s[3:0]), .wb_s(wb_s), .R_Wb(R_Wb), .CE(dec_3to8_1_line_s[5]),
    .rb_s(rb_s));
  sram_16wOpt sram_16wopt_7 (
    .addr_valid(addr_valid), .addr4b_s(addr8b_s[3:0]), .wb_s(wb_s), .R_Wb(R_Wb), .CE(dec_3to8_1_line_s[6]),
    .rb_s(rb_s));
  sram_16wOpt sram_16wopt_8 (
    .addr_valid(addr_valid), .addr4b_s(addr8b_s[3:0]), .wb_s(wb_s), .R_Wb(R_Wb), .CE(dec_3to8_1_line_s[7]),
    .rb_s(rb_s));

  // Notes on the sheet:
  //   CE: initial=0x1
  //   addr_valid: initial=0x1
  //   address bus is 8bits deep
endmodule

module ram_progV2 (
  input  [7:0] A1_8b,
  input  INIT,
  input  PROG,
  input  R_Wb,
  input  [15:0] WD2_16b,
  input  clk,
  input  [7:0] A2_8b,
  output [15:0] R1,
  output pInProgess,
  output [15:0] R2
);

  wire and_1_out, and_2_out, buffer_1_out, jk_flipflop_v2_1_q, nand_1_out, not_1_out, not_2_out, not_4_out,
       not_5_out, program_counter_8b_1_ffoverflow;
  wire [7:0] controlled_buffer_1_out, controlled_buffer_3_out, program_counter_8b_1_counted;
  wire [15:0] controlled_buffer_5_out, rom_1_data;

  buf buffer_1 (buffer_1_out, PROG);
  not not_1 (not_1_out, PROG);
  not not_2 (not_2_out, INIT);
  not not_3 (pInProgess, jk_flipflop_v2_1_q);
  program_counter_8b program_counter_8b_1 (
    .clk(clk), .COUNTEN(buffer_1_out), .LOADEN(jk_flipflop_v2_1_q), .L_s({8{1'b0}}), .sRst_b(not_2_out),
    .ffOverflow(program_counter_8b_1_ffoverflow), .COUNTED(program_counter_8b_1_counted));
  jk_flipflop_V2 jk_flipflop_v2_1 (
    .J(program_counter_8b_1_ffoverflow), .K(program_counter_8b_1_ffoverflow), .clk(clk), .sRst_b(not_2_out),
    .Q(jk_flipflop_v2_1_q));  // open: Q_b
  not not_4 (not_4_out, clk);
  assign controlled_buffer_1_out = not_1_out ? A1_8b : 8'bz;  // Controlled_Buffer controlled_buffer_1
  assign controlled_buffer_1_out = buffer_1_out ? program_counter_8b_1_counted : 8'bz;  // Controlled_Buffer controlled_buffer_2
  assign controlled_buffer_3_out = buffer_1_out ? program_counter_8b_1_counted : 8'bz;  // Controlled_Buffer controlled_buffer_3
  assign controlled_buffer_3_out = not_1_out ? A2_8b : 8'bz;  // Controlled_Buffer controlled_buffer_4
  not not_5 (not_5_out, controlled_buffer_1_out[7]);
  sram_128wOpt sram_128wopt_1 (
    .CE(not_5_out), .addr8b_s(controlled_buffer_1_out), .addr_valid(not_4_out), .wb_s(rom_1_data),
    .R_Wb(not_1_out), .rb_s(R1));
  sram_128wOpt sram_128wopt_2 (
    .CE(and_2_out), .addr8b_s(controlled_buffer_3_out), .addr_valid(not_4_out),
    .wb_s(controlled_buffer_5_out), .R_Wb(and_1_out), .rb_s(R2));
  ROM #(.dataWidth(16)) rom_1 (.addr(controlled_buffer_1_out), .data(rom_1_data));
  assign controlled_buffer_5_out = buffer_1_out ? rom_1_data : 16'bz;  // Controlled_Buffer controlled_buffer_5
  and and_1 (and_1_out, not_1_out, R_Wb);
  assign controlled_buffer_5_out = not_1_out ? WD2_16b : 16'bz;  // Controlled_Buffer controlled_buffer_6
  and and_2 (and_2_out, controlled_buffer_3_out[7], nand_1_out);
  nand nand_1 (nand_1_out, controlled_buffer_3_out[6], controlled_buffer_3_out[5], controlled_buffer_3_out[4]);

  // Notes on the sheet:
  //   PROG: initial=0x1
  //   contents of rom_1 (hex, n*v repeats v):
  //   0 2d9e e201 80 c01d c11e 200b e207 8 e205 1 e20f f0 e004 62 29e5 8002 20d6 a001 2006 60ee 50dd bb6
  //   bff7 8ff4 d0fb a7ff 69*0 5555 aaaa 14*0 d0f7 b014 14*0 fd c5
  //   exclude last 16w block from writtable addresses
  //    (i.e., [0xf0 - 0xff] is A2_8b no-avail range)
endmodule

module core_V2 (
  input  INIT,
  input  FLASH,
  input  RAMWrite,
  input  REGCapture,
  input  newInstr,
  input  PCCapture_O,
  input  RegWrite,
  input  R1orPC,
  input  [2:0] aluControl,
  input  ALUCapture,
  input  PCload,
  input  PCount,
  input  src1InSrc2,
  input  updateFlags,
  input  R2orSE,
  input  dstInSrc2,
  input  [1:0] writeSrc,
  input  [15:0] RD2_BUS,
  input  R1Capture_O,
  input  clk,
  input  MEMCapture,
  input  [1:0] R0_R1w_R2w_i2,
  output [3:0] ALUflags,
  output pcOV,
  output beingProged,
  output [7:0] AD2_BUS,
  output [7:0] opcode,
  output dst0,
  output [15:0] WD2_BUS
);

  wire nor_1_out, not_1_out, not_2_out, not_3_out;
  wire [3:0] alu_fullv1_1_alu_flags, AW_q_4, multiplexer_1_out, multiplexer_2_out;
  wire [7:0] alu_res_p_q_16, alu_res_p_q_16_2, alu_res_q_16, MIR_q_16, program_counter_8b_1_counted;
  wire [15:0] alu_fullv1_1_alu_out, bit_extender_1_out, bit_extender_2_out, bit_extender_3_out,
       bit_extender_4_out, multiplexer_3_out, multiplexer_4_out, multiplexer_5_out, multiplexer_6_out,
       PC_q_16, R1_q_16, R1p_q_16, RAM2_q_16, ram_progv2_1_r1, regf_full16_1_rd1, regf_full16_1_rd2, SE_q_16;

  // NoConnect on alu_res_p_q_16_2
  not not_1 (not_1_out, INIT);
  nor nor_1 (nor_1_out, INIT, FLASH);
  program_counter_8b program_counter_8b_1 (
    .clk(clk), .COUNTEN(PCount), .LOADEN(PCload), .L_s(alu_res_p_q_16), .sRst_b(nor_1_out),
    .ffOverflow(pcOV), .COUNTED(program_counter_8b_1_counted));
  LED led_1 (.in(pcOV));
  // NoConnect on alu_res_q_16
  assign bit_extender_1_out = {{8{1'b0}}, program_counter_8b_1_counted};  // Bit_Extender bit_extender_1
  not not_2 (not_2_out, RAMWrite);
  ram_progV2 ram_progv2_1 (
    .PROG(FLASH), .clk(clk), .INIT(INIT), .A1_8b(program_counter_8b_1_counted), .A2_8b(AD2_BUS),
    .WD2_16b(WD2_BUS), .R_Wb(not_2_out), .pInProgess(beingProged), .R1(ram_progv2_1_r1), .R2(RD2_BUS));
  LED led_2 (.in(beingProged));
  nor nor_2 (dst0, opcode[0], opcode[1], opcode[2], opcode[3]);
  Dff_16b MIR (.EN(newInstr), .clk(clk), .D_16(ram_progv2_1_r1), .sRst_b(not_1_out), .Q_16({opcode, MIR_q_16}));
  Dff_16b PC (.EN(PCCapture_O), .clk(clk), .D_16(bit_extender_1_out), .sRst_b(not_1_out), .Q_16(PC_q_16));
  Dff_16b RAM2 (.EN(MEMCapture), .clk(clk), .D_16(RD2_BUS), .sRst_b(not_1_out), .Q_16(RAM2_q_16));
  Multiplexer #(.width(4)) multiplexer_1 (
    .in0(MIR_q_16[7:4]), .in1(MIR_q_16[3:0]), .out(multiplexer_1_out), .sel(src1InSrc2));
  Multiplexer #(.width(4)) multiplexer_2 (
    .in0(opcode[3:0]), .in1(MIR_q_16[3:0]), .out(multiplexer_2_out), .sel(dstInSrc2));
  Dff_16b alu_res_p (
    .EN(MEMCapture), .clk(clk), .D_16({alu_res_q_16, AD2_BUS}), .sRst_b(not_1_out),
    .Q_16({alu_res_p_q_16_2, alu_res_p_q_16}));
  assign bit_extender_2_out = {{5{opcode[2]}}, {opcode[2:0], MIR_q_16}};  // Bit_Extender bit_extender_2
  assign bit_extender_3_out = {{12{opcode[3]}}, opcode[3:0]};  // Bit_Extender bit_extender_3
  assign bit_extender_4_out = {{9{opcode[2]}}, {opcode[2:0], MIR_q_16[7:4]}};  // Bit_Extender bit_extender_4
  Dff_4b AW (.clk(clk), .EN(REGCapture), .sRst_b(not_1_out), .D_4(multiplexer_2_out), .Q_4(AW_q_4));
  Multiplexer #(.select(2), .width(16)) multiplexer_3 (
    .in0(PC_q_16), .in1(RAM2_q_16), .in2({alu_res_p_q_16_2, alu_res_p_q_16}), .in3(R1p_q_16),
    .out(multiplexer_3_out));  // open: sel
  Dff_16b R1p (.EN(R1Capture_O), .clk(clk), .D_16(R1_q_16), .sRst_b(not_1_out), .Q_16(R1p_q_16));
  not not_3 (not_3_out, clk);
  regf_Full16 regf_full16_1 (
    .AR2(MIR_q_16[3:0]), .AR1(multiplexer_1_out), .WD(multiplexer_3_out), .INIT(INIT), .WE(RegWrite),
    .addr_valid(not_3_out), .AW(AW_q_4), .RD1(regf_full16_1_rd1), .RD2(regf_full16_1_rd2));
  Multiplexer #(.select(2), .width(16)) multiplexer_4 (
    .in0(bit_extender_2_out), .in1(bit_extender_3_out), .in2(bit_extender_4_out), .in3(ram_progv2_1_r1),
    .out(multiplexer_4_out));  // open: sel
  Dff_16b R1 (.EN(REGCapture), .clk(clk), .D_16(regf_full16_1_rd1), .sRst_b(not_1_out), .Q_16(R1_q_16));
  Dff_16b R2 (.EN(REGCapture), .clk(clk), .D_16(regf_full16_1_rd2), .sRst_b(not_1_out), .Q_16(WD2_BUS));
  Dff_16b SE (.EN(REGCapture), .clk(clk), .D_16(multiplexer_4_out), .sRst_b(not_1_out), .Q_16(SE_q_16));
  Multiplexer #(.width(16)) multiplexer_5 (.in0(R1_q_16), .in1(PC_q_16), .out(multiplexer_5_out), .sel(R1orPC));
  Multiplexer #(.width(16)) multiplexer_6 (.in0(WD2_BUS), .in1(SE_q_16), .out(multiplexer_6_out), .sel(R2orSE));
  alu_fullv1 alu_fullv1_1 (
    .ctrl({1'b0, aluControl}), .B(multiplexer_6_out), .A(multiplexer_5_out), .alu_out(alu_fullv1_1_alu_out),
    .alu_flags(alu_fullv1_1_alu_flags));
  Dff_4b dff_4b_1 (.clk(clk), .EN(updateFlags), .sRst_b(not_1_out), .D_4(alu_fullv1_1_alu_flags), .Q_4(ALUflags));
  Dff_16b alu_res (
    .EN(ALUCapture), .clk(clk), .D_16(alu_fullv1_1_alu_out), .sRst_b(not_1_out),
    .Q_16({alu_res_q_16, AD2_BUS}));

  // Notes on the sheet:
  //   FLASH: initial=0x1
  //   INIT: initial=0x1
  //   R0
  //   R1w
  //   R2w
  //   pc'
  //   ram out
  //   alu out
  //   R1
endmodule

module regf_Full16 (
  input  INIT,
  input  [15:0] WD,
  input  addr_valid,
  input  WE,
  input  [3:0] AR2,
  input  [3:0] AW,
  input  [3:0] AR1,
  output [15:0] RD1,
  output [15:0] RD2
);

  wire and_1_out, not_1_out;
  wire [15:0] d_latch_16b_1_q, dec_4to16_1_line_s, dec_4to16_2_line_s, dec_4to16_3_line_s, or_1_out;

  Dec_4to16 dec_4to16_1 (.b2(AR2[2]), .b1(AR2[1]), .b0(AR2[0]), .EN(1'b1), .b3(AR2[3]), .Line_s(dec_4to16_1_line_s));
  Dec_4to16 dec_4to16_2 (.b2(AR1[2]), .b1(AR1[1]), .b0(AR1[0]), .EN(1'b1), .b3(AR1[3]), .Line_s(dec_4to16_2_line_s));
  not not_1 (not_1_out, INIT);
  D_latch_16b d_latch_16b_1 (.EN(and_1_out), .sClr_b(not_1_out), .D(WD), .Q(d_latch_16b_1_q));
  regf_s0 regf_s0_1 (.RE1(dec_4to16_2_line_s[0]), .RE2(dec_4to16_1_line_s[0]), .rb1_s(RD1), .rb2_s(RD2));
  regf_1w_Dual Reg4 (
    .WE(or_1_out[3]), .RE1(dec_4to16_2_line_s[3]), .RE2(dec_4to16_1_line_s[3]), .wb_s(d_latch_16b_1_q),
    .rb1_s(RD1), .rb2_s(RD2));
  regf_1w_Dual Reg7 (
    .WE(or_1_out[6]), .RE1(dec_4to16_2_line_s[6]), .RE2(dec_4to16_1_line_s[6]), .wb_s(d_latch_16b_1_q),
    .rb1_s(RD1), .rb2_s(RD2));
  regf_1w_Dual Reg10 (
    .WE(or_1_out[9]), .RE1(dec_4to16_2_line_s[9]), .RE2(dec_4to16_1_line_s[9]), .wb_s(d_latch_16b_1_q),
    .rb1_s(RD1), .rb2_s(RD2));
  regf_1w_Dual reg13 (
    .WE(or_1_out[12]), .RE1(dec_4to16_2_line_s[12]), .RE2(dec_4to16_1_line_s[12]), .wb_s(d_latch_16b_1_q),
    .rb1_s(RD1), .rb2_s(RD2));
  regf_1w_Dual Reg2 (
    .WE(or_1_out[1]), .RE1(dec_4to16_2_line_s[1]), .RE2(dec_4to16_1_line_s[1]), .wb_s(d_latch_16b_1_q),
    .rb1_s(RD1), .rb2_s(RD2));
  regf_1w_Dual Reg5 (
    .WE(or_1_out[4]), .RE1(dec_4to16_2_line_s[4]), .RE2(dec_4to16_1_line_s[4]), .wb_s(d_latch_16b_1_q),
    .rb1_s(RD1), .rb2_s(RD2));
  regf_1w_Dual Reg8 (
    .WE(or_1_out[7]), .RE1(dec_4to16_2_line_s[7]), .RE2(dec_4to16_1_line_s[7]), .wb_s(d_latch_16b_1_q),
    .rb1_s(RD1), .rb2_s(RD2));
  regf_1w_Dual Reg11 (
    .WE(or_1_out[10]), .RE1(dec_4to16_2_line_s[10]), .RE2(dec_4to16_1_line_s[10]), .wb_s(d_latch_16b_1_q),
    .rb1_s(RD1), .rb2_s(RD2));
  regf_1w_Dual reg14 (
    .WE(or_1_out[13]), .RE1(dec_4to16_2_line_s[13]), .RE2(dec_4to16_1_line_s[13]), .wb_s(d_latch_16b_1_q),
    .rb1_s(RD1), .rb2_s(RD2));
  regf_1w_Dual reg16 (
    .WE(or_1_out[15]), .RE1(dec_4to16_2_line_s[15]), .RE2(dec_4to16_1_line_s[15]), .wb_s(d_latch_16b_1_q),
    .rb1_s(RD1), .rb2_s(RD2));
  regf_1w_Dual Reg3 (
    .WE(or_1_out[2]), .RE1(dec_4to16_2_line_s[2]), .RE2(dec_4to16_1_line_s[2]), .wb_s(d_latch_16b_1_q),
    .rb1_s(RD1), .rb2_s(RD2));
  regf_1w_Dual Reg6 (
    .WE(or_1_out[5]), .RE1(dec_4to16_2_line_s[5]), .RE2(dec_4to16_1_line_s[5]), .wb_s(d_latch_16b_1_q),
    .rb1_s(RD1), .rb2_s(RD2));
  regf_1w_Dual Reg9 (
    .WE(or_1_out[8]), .RE1(dec_4to16_2_line_s[8]), .RE2(dec_4to16_1_line_s[8]), .wb_s(d_latch_16b_1_q),
    .rb1_s(RD1), .rb2_s(RD2));
  regf_1w_Dual Reg12 (
    .WE(or_1_out[11]), .RE1(dec_4to16_2_line_s[11]), .RE2(dec_4to16_1_line_s[11]), .wb_s(d_latch_16b_1_q),
    .rb1_s(RD1), .rb2_s(RD2));
  regf_1w_Dual reg15 (
    .WE(or_1_out[14]), .RE1(dec_4to16_2_line_s[14]), .RE2(dec_4to16_1_line_s[14]), .wb_s(d_latch_16b_1_q),
    .rb1_s(RD1), .rb2_s(RD2));
  assign or_1_out = {16{INIT}} | dec_4to16_3_line_s;  // OR_Gate or_1, 16 bits wide
  and and_1 (and_1_out, WE, addr_valid);
  Dec_4to16 dec_4to16_3 (.b2(AW[2]), .b1(AW[1]), .b0(AW[0]), .EN(and_1_out), .b3(AW[3]), .Line_s(dec_4to16_3_line_s));

  // Notes on the sheet:
  //   INIT: initial=0x1
endmodule

module testall_wlogic_V2 (
  input  FLASH,
  input  INIT
);

  wire and_1_out, and_2_out, and_3_out, and_4_out, and_5_out, and_6_out, and_7_out, and_8_out, and_9_out,
       and_10_out, and_11_out, and_12_out, and_13_out, branch_taker_4b_1_donttake, branch_taker_4b_1_take,
       clk_out, core_v2_1_beingproged, core_v2_1_dst0, handles_puller_v2_1_branchrqst,
       handles_puller_v2_1_dstinsrc2, handles_puller_v2_1_pccapture, handles_puller_v2_1_pccount,
       handles_puller_v2_1_pcload, handles_puller_v2_1_r1capture, handles_puller_v2_1_r1orpc,
       handles_puller_v2_1_r2orse, handles_puller_v2_1_ramwrite, handles_puller_v2_1_regwrite,
       handles_puller_v2_1_src1insrc2, handles_puller_v2_1_updateflags, multiplexer_1_out, not_1_out,
       or_1_out, program_counter_4b_1_rcout;
  wire [1:0] handles_puller_v2_1_sesrc, handles_puller_v2_1_writesrc;
  wire [2:0] handles_puller_v2_1_aluctrls;
  wire [3:0] core_v2_1_aluflags, dff_16b_1_q_16, dff_16b_1_q_16_2, dff_16b_1_q_16_3,
       program_counter_4b_1_cout_s;
  wire [7:0] core_v2_1_ad2_bus, core_v2_1_opcode, dec_3to8_1_line_s;
  wire [15:0] core_v2_1_wd2_bus;
  wire [15:12] dff_16b_1_q_16_4;

  Hex_Digit_Display hex_digit_display_1 (.value(dff_16b_1_q_16_4));  // open: dp
  Hex_Digit_Display hex_digit_display_2 (.value(dff_16b_1_q_16_3));  // open: dp
  Hex_Digit_Display hex_digit_display_3 (.value(dff_16b_1_q_16_2));  // open: dp
  and and_1 (and_1_out, core_v2_1_ad2_bus[5], core_v2_1_ad2_bus[4]);
  and and_2 (and_2_out, and_1_out, and_3_out);
  and and_3 (and_3_out, core_v2_1_ad2_bus[7], core_v2_1_ad2_bus[6]);
  Clock clk (.out(clk_out));
  LED led_1 (.in(core_v2_1_beingproged));
  not not_1 (not_1_out, INIT);
  Hex_Digit_Display hex_digit_display_4 (.value(dff_16b_1_q_16));  // open: dp
  Dff_16b dff_16b_1 (
    .EN(and_4_out), .clk(clk_out), .D_16(core_v2_1_wd2_bus), .sRst_b(not_1_out),
    .Q_16({dff_16b_1_q_16_4, dff_16b_1_q_16_3, dff_16b_1_q_16_2, dff_16b_1_q_16}));
  and and_4 (and_4_out, and_2_out, and_10_out);
  and and_5 (and_5_out, dec_3to8_1_line_s[1], handles_puller_v2_1_pccount);
  and and_6 (and_6_out, dec_3to8_1_line_s[1], handles_puller_v2_1_pccapture);
  handles_puller_V2 handles_puller_v2_1 (
    .opCode(core_v2_1_opcode), .dst0(core_v2_1_dst0), .branchRqst(handles_puller_v2_1_branchrqst),
    .PCCapture(handles_puller_v2_1_pccapture), .PCCount(handles_puller_v2_1_pccount),
    .src1InSrc2(handles_puller_v2_1_src1insrc2), .dstInSrc2(handles_puller_v2_1_dstinsrc2),
    .SESrc(handles_puller_v2_1_sesrc), .R1Capture(handles_puller_v2_1_r1capture),
    .R1orPC(handles_puller_v2_1_r1orpc), .R2orSE(handles_puller_v2_1_r2orse),
    .ALUCtrls(handles_puller_v2_1_aluctrls), .updateFlags(handles_puller_v2_1_updateflags),
    .RAMWrite(handles_puller_v2_1_ramwrite), .WriteSrc(handles_puller_v2_1_writesrc),
    .REGWrite(handles_puller_v2_1_regwrite), .PCLoad(handles_puller_v2_1_pcload));
  and and_7 (and_7_out, dec_3to8_1_line_s[2], handles_puller_v2_1_r1capture);
  and and_8 (and_8_out, handles_puller_v2_1_updateflags, dec_3to8_1_line_s[2]);
  and and_9 (and_9_out, handles_puller_v2_1_regwrite, dec_3to8_1_line_s[4]);
  and and_10 (and_10_out, handles_puller_v2_1_ramwrite, dec_3to8_1_line_s[3]);
  core_V2 core_v2_1 (
    .clk(clk_out), .aluControl(handles_puller_v2_1_aluctrls), .PCload(multiplexer_1_out), .PCount(or_1_out),
    .FLASH(FLASH), .updateFlags(and_8_out), .ALUCapture(dec_3to8_1_line_s[2]), .RAMWrite(and_10_out),
    .INIT(INIT), .MEMCapture(dec_3to8_1_line_s[3]), .newInstr(dec_3to8_1_line_s[0]), .PCCapture_O(and_6_out),
    .src1InSrc2(handles_puller_v2_1_src1insrc2), .dstInSrc2(handles_puller_v2_1_dstinsrc2),
    .R1Capture_O(and_7_out), .writeSrc(handles_puller_v2_1_writesrc), .RegWrite(and_9_out),
    .R0_R1w_R2w_i2(handles_puller_v2_1_sesrc), .REGCapture(dec_3to8_1_line_s[1]),
    .R2orSE(handles_puller_v2_1_r2orse), .R1orPC(handles_puller_v2_1_r1orpc), .ALUflags(core_v2_1_aluflags),
    .AD2_BUS(core_v2_1_ad2_bus), .WD2_BUS(core_v2_1_wd2_bus), .beingProged(core_v2_1_beingproged),
    .dst0(core_v2_1_dst0), .opcode(core_v2_1_opcode));  // open: RD2_BUS, pcOV
  or or_1 (or_1_out, and_5_out, dec_3to8_1_line_s[0]);
  branch_taker_4B branch_taker_4b_1 (
    .BranchOpCode(core_v2_1_opcode[5:3]), .BranchRequest(handles_puller_v2_1_branchrqst),
    .ALUflags(core_v2_1_aluflags), .take(branch_taker_4b_1_take), .donttake(branch_taker_4b_1_donttake));
  and and_11 (and_11_out, handles_puller_v2_1_pcload, dec_3to8_1_line_s[4]);
  Multiplexer multiplexer_1 (
    .in0(and_11_out), .in1(and_12_out), .out(multiplexer_1_out), .sel(handles_puller_v2_1_branchrqst));
  and and_12 (and_12_out, and_11_out, branch_taker_4b_1_take);
  and and_13 (and_13_out, ~FLASH, not_1_out);  // AND_Gate
  program_counter_4b program_counter_4b_1 (
    .COUNTEN(1'b1), .L_s(4'b0000), .LOADEN(dec_3to8_1_line_s[4]), .clk(clk_out), .sRst_b(and_13_out),
    .cOut_s(program_counter_4b_1_cout_s), .rcOut(program_counter_4b_1_rcout));
  // NoConnect on program_counter_4b_1_rcout
  // NoConnect on branch_taker_4b_1_donttake
  Dec_3to8 dec_3to8_1 (
    .b2(program_counter_4b_1_cout_s[2]), .b1(program_counter_4b_1_cout_s[1]),
    .b0(program_counter_4b_1_cout_s[0]), .CE(1'b1), .Line_s(dec_3to8_1_line_s));

  // Notes on the sheet:
  //   FLASH: initial=0x1
  //   INIT: initial=0x1
  //   read from addr
  //   pccount
  //   D
  //   Ex
  //   Mem
  //   WB
endmodule

module branch_taker_4B (
  input  [3:0] ALUflags,
  input  BranchRequest,
  input  [2:0] BranchOpCode,
  output donttake,
  output take
);

  wire and_1_out, and_2_out, and_3_out, and_4_out, and_5_out, or_1_out, or_2_out;
  wire [7:0] dec_3to8_1_line_s;

  Dec_3to8 dec_3to8_1 (
    .b2(BranchOpCode[2]), .b1(BranchOpCode[1]), .b0(BranchOpCode[0]), .CE(BranchRequest),
    .Line_s(dec_3to8_1_line_s));
  and and_1 (and_1_out, ALUflags[0], dec_3to8_1_line_s[0]);
  and and_2 (and_2_out, ~ALUflags[0], dec_3to8_1_line_s[1]);  // AND_Gate
  and and_3 (and_3_out, ALUflags[2], dec_3to8_1_line_s[2]);
  or or_1 (or_1_out, ALUflags[0], ALUflags[2]);
  and and_4 (and_4_out, or_1_out, dec_3to8_1_line_s[3]);
  and and_5 (and_5_out, ALUflags[3], dec_3to8_1_line_s[5]);
  or or_2 (or_2_out, and_1_out, and_2_out, and_3_out, and_4_out, and_5_out);
  and and_6 (take, or_2_out, BranchRequest);
  and and_7 (donttake, ~or_2_out, BranchRequest);  // AND_Gate

  // Notes on the sheet:
  //   Branch
  //   BNZ
  //   BLT
  //   BLE
  //   BCF
  //   BZ
  //   CF |LTF | NF | ZF
  //   take
  //   don't take
endmodule

module handles_puller_V2 (
  input  [7:0] opCode,
  input  dst0,
  output branchRqst,
  output PCCount,
  output dstInSrc2,
  output R1Capture,
  output R2orSE,
  output updateFlags,
  output [1:0] WriteSrc,
  output PCLoad,
  output PCCapture,
  output src1InSrc2,
  output [1:0] SESrc,
  output R1orPC,
  output [2:0] ALUCtrls,
  output RAMWrite,
  output REGWrite
);

  wire and_1_out, or_2_out, rom1R1I_out, rom2W_out, romB_out, romJI_out, romMEM_out, romR2_out, romR3_out;
  wire [2:0] enc_8to3_1_y;
  wire [8:6] my2W_data_2;
  wire [19:0] my1R1I_data, my2W_data, myMEM_data, myR2_data;
  wire [19:18] multiplexer_1_out;

  and romB (romB_out, opCode[7], ~opCode[6], ~opCode[5]);  // AND_Gate
  and romJI (romJI_out, opCode[7], ~opCode[6], opCode[5], ~opCode[4]);  // AND_Gate
  nor romR3 (romR3_out, dst0, opCode[7]);
  and romR2 (romR2_out, ~opCode[7], dst0);  // AND_Gate
  or or_1 (branchRqst, romB_out, and_1_out);
  or or_2 (or_2_out, romB_out, romJI_out);
  and and_1 (and_1_out, romJI_out, opCode[3]);
  and romMEM (romMEM_out, opCode[7], opCode[6], ~opCode[5]);  // AND_Gate
  and rom1R1I (rom1R1I_out, opCode[7], ~opCode[6], opCode[5], opCode[4]);  // AND_Gate
  and rom2W (rom2W_out, opCode[7], opCode[6], opCode[5]);
  Enc_8to3 enc_8to3_1 (
    .L7(1'b0), .L6(1'b0), .L5(rom2W_out), .L4(rom1R1I_out), .L3(romMEM_out), .L2(or_2_out), .L1(romR2_out),
    .L0(romR3_out), .Y(enc_8to3_1_y));
  ROM #(.addrWidth(3), .dataWidth(20)) myR2 (.addr(opCode[6:4]), .data(myR2_data));
  ROM #(.addrWidth(2), .dataWidth(20)) myMEM (.addr({1'b0, opCode[4]}), .data(myMEM_data));
  ROM #(.addrWidth(2), .dataWidth(20)) my1R1I (.addr({1'b0, opCode[3]}), .data(my1R1I_data));
  ROM #(.addrWidth(2), .dataWidth(20)) my2W (.addr(opCode[1:0]), .data({my2W_data[19:9], my2W_data_2, my2W_data[5:0]}));
  Multiplexer #(.select(3), .width(20)) multiplexer_1 (
    .in0({{11{1'b0}}, opCode[6:4], 6'b101010}), .in1(myR2_data), .in2(20'h20601), .in3(myMEM_data),
    .in4(my1R1I_data), .in5({my2W_data[19:9], opCode[4:2], my2W_data[5:0]}), .in6({20{1'b0}}),
    .in7({20{1'b0}}),
    .out({multiplexer_1_out, PCCapture, PCCount, src1InSrc2, dstInSrc2, SESrc, R1Capture, R1orPC, R2orSE, ALUCtrls, updateFlags, RAMWrite, WriteSrc, REGWrite, PCLoad}),
    .sel(enc_8to3_1_y));
  // NoConnect on my2W_data_2[8]
  // NoConnect on my2W_data_2[7]
  // NoConnect on my2W_data_2[6]

  // Notes on the sheet:
  //   15 14 13 12
  //   11
  //   contents of myR2 (hex, n*v repeats v):
  //   0 20 480e 0 0 414a 418a 41ca
  //   contents of myMEM (hex, n*v repeats v):
  //   5206 5210
  //   contents of my1R1I (hex, n*v repeats v):
  //   a201 e22a
  //   contents of my2W (hex, n*v repeats v):
  //   37603 1722a 1720a 13220
  //   romR3
  //   romR2
  //   romBRANCH
  //   romJI
  //   romMEM
  //   rom1REG1IMM
  //   rom2W
endmodule

module Enc_8to3 (
  input  L7,
  input  L6,
  input  L5,
  input  L4,
  input  L3,
  input  L2,
  input  L1,
  input  L0,
  output [2:0] Y
);

  // NoConnect on L0
  or or_1 (Y[2], L4, L5, L6, L7);
  or or_2 (Y[1], L2, L3, L6, L7);
  or or_3 (Y[0], L1, L3, L5, L7);

  // Notes on the sheet:
  //   Address Encoder 8 lines to 3 bits
  //   Y2
  //   Y1
  //   Y0
endmodule
